// Logisim project alu.circ as structural Verilog: 6 circuits, main circuit alu
module alu (
  input  [31:0] A,
  input  [31:0] B,
  input  [3:0] ALUSel,
  output [31:0] Result
);

  wire [0:0] comparator_1_lt, comparator_2_eq;
  wire [5:0] adder_2_out, bitadder_1_out, bitadder_2_out;
  wire [31:0] adder_1_out, and_1_out, div_1_out_3, divider_1_out, divider_1_rem, mulh_1_out_3,
       multiplier_1_cout, multiplier_1_out, or_1_out, reverse_1_out_2, shifter_1_out, shifter_2_out,
       subtractor_1_out, xor_1_out;

  assign and_1_out = A & B;  // AND_Gate and_1, 32 bits wide
  assign or_1_out = A | B;  // OR_Gate or_1, 32 bits wide
  assign xor_1_out = A ^ B;  // XOR_Gate xor_1, 32 bits wide
  Adder #(.width(32)) adder_1 (.a(A), .b(B), .out(adder_1_out));  // open: cin, cout
  Subtractor #(.width(32)) subtractor_1 (.a(A), .b(B), .out(subtractor_1_out));  // open: bin, bout
  Multiplier #(.width(32)) multiplier_1 (.a(A), .b(B), .out(multiplier_1_out), .cout(multiplier_1_cout));  // open: cin
  mulh mulh_1 (.A(A), .B(B), .out_3(mulh_1_out_3));
  Divider #(.width(32)) divider_1 (.a(A), .b(B), .out(divider_1_out), .rem(divider_1_rem));  // open: upper
  div div_1 (.in_1(A), .in_2(B), .out_3(div_1_out_3));
  Comparator #(.width(32)) comparator_1 (.a(A), .b(B), .lt(comparator_1_lt[0]));  // open: gt, eq
  Shifter #(.width(32), .shift("lr")) shifter_1 (.in(A), .\dist (B[4:0]), .out(shifter_1_out));
  Shifter #(.width(32), .shift("ar")) shifter_2 (.in(A), .\dist (B[4:0]), .out(shifter_2_out));
  reverse reverse_1 (.in_1(A), .out_2(reverse_1_out_2));
  BitAdder #(.width(32)) bitadder_1 (.in0(A), .out(bitadder_1_out));
  BitAdder #(.width(32)) bitadder_2 (.in0(B), .out(bitadder_2_out));
  Comparator #(.width(32)) comparator_2 (.a(reverse_1_out_2), .b(B), .eq(comparator_2_eq[0]));  // open: gt, lt
  Adder #(.width(6)) adder_2 (.a(bitadder_1_out), .b(bitadder_2_out), .out(adder_2_out));  // open: cin, cout
  Multiplexer #(.select(4), .width(32), .enable("false")) multiplexer_1 (
    .in0(and_1_out), .in1(or_1_out), .in2(xor_1_out), .in3(adder_1_out), .in4(subtractor_1_out),
    .in5(multiplier_1_out), .in6(multiplier_1_cout), .in7(mulh_1_out_3), .in8(divider_1_out),
    .in9(div_1_out_3), .in10(divider_1_rem), .in11(shifter_1_out), .in12(shifter_2_out),
    .in13({{31{1'b0}}, comparator_1_lt[0]}), .in14({{31{1'b0}}, comparator_2_eq[0]}),
    .in15({{26{1'b0}}, adder_2_out}), .out(Result), .sel(ALUSel));

  // Notes on the sheet:
  //   INPUTS to your circuit
  //   DON'T CHANGE THE LOCATIONS OF THE INPUTS AND OUTPUTS!
  //   OUTPUT from your circuit
endmodule

module mulh (
  input  [31:0] A,
  input  [31:0] B,
  output [31:0] out_3
);

  wire [31:0] multiplier_1_out, multiplier_2_cout, multiplier_3_out, subtractor_1_out;

  // Probe on {{31{1'b0}}, A[31]}
  // Probe on multiplier_3_out
  // Probe on multiplier_2_cout
  Multiplier #(.width(32)) multiplier_1 (
    .a({1'b0, B[30:0]}), .b({{31{1'b0}}, A[31]}), .out(multiplier_1_out));  // open: cin, cout
  Multiplier #(.width(32)) multiplier_2 (.a(A), .b(B), .cout(multiplier_2_cout));  // open: out, cin
  Multiplier #(.width(32)) multiplier_3 (
    .a({1'b0, A[30:0]}), .b({{31{1'b0}}, B[31]}), .out(multiplier_3_out));  // open: cin, cout
  // Probe on multiplier_1_out
  Subtractor #(.width(32)) subtractor_1 (
    .a(multiplier_2_cout), .b(multiplier_3_out), .out(subtractor_1_out));  // open: bin, bout
  // Probe on subtractor_1_out
  Subtractor #(.width(32)) subtractor_2 (.a(subtractor_1_out), .b(multiplier_1_out), .out(out_3));  // open: bin, bout
endmodule

module div (
  input  [31:0] in_1,
  input  [31:0] in_2,
  output [31:0] out_3
);

  wire [1:0] slt0_1_out_2;
  wire [31:0] adder_1_out, ANBN, ANBP, APBN, APBP, multiplexer_1_out, negator_1_out, subtractor_1_out,
       subtractor_2_out;

  Subtractor #(.width(32)) subtractor_1 (.a({32{1'b0}}), .b(in_1), .out(subtractor_1_out));  // open: bin, bout
  Subtractor #(.width(32)) subtractor_2 (.a({32{1'b0}}), .b(in_2), .out(subtractor_2_out));  // open: bin, bout
  slt0 slt0_1 (.in_1(in_1), .out_2(slt0_1_out_2[0]));
  slt0 slt0_2 (.in_1(in_2), .out_2(slt0_1_out_2[1]));
  Divider #(.width(32)) divider_1 (.a(in_1), .b(subtractor_2_out), .out(APBN));  // open: upper, rem
  Divider #(.width(32)) divider_2 (.a(subtractor_1_out), .b(subtractor_2_out), .out(ANBN));  // open: upper, rem
  Divider #(.width(32)) divider_3 (.a(subtractor_1_out), .b(in_2), .out(ANBP));  // open: upper, rem
  Divider #(.width(32)) divider_4 (.a(in_1), .b(in_2), .out(APBP));  // open: upper, rem
  Multiplexer #(.select(2), .width(32), .enable("false")) multiplexer_1 (
    .in1(ANBP), .in2(APBN), .out(multiplexer_1_out), .sel(slt0_1_out_2));  // open: in0, in3
  Multiplexer #(.select(2), .width(32), .enable("false")) multiplexer_2 (
    .in0(APBP), .in1(negator_1_out), .in2(negator_1_out), .in3(ANBN), .out(out_3), .sel(slt0_1_out_2));
  Adder #(.width(32)) adder_1 (.a({32{1'b0}}), .b(multiplexer_1_out), .out(adder_1_out));  // open: cin, cout
  Negator #(.width(32)) negator_1 (.in(adder_1_out), .out(negator_1_out));

  // Other names for the same wires on the sheet: A[31:0] = in_1; B[31:0] = in_2
endmodule

module slt (
  input  [31:0] in_1,
  input  [31:0] in_2,
  output out_3
);

  wire slt0_1_out_2, slt0_2_out_2, slt0_3_out_2, xor_1_out;
  wire [31:0] subtractor_1_out;

  slt0 slt0_1 (.in_1(in_1), .out_2(slt0_1_out_2));
  Subtractor #(.width(32)) subtractor_1 (.a(in_1), .b(in_2), .out(subtractor_1_out));  // open: bin, bout
  slt0 slt0_2 (.in_1(in_2), .out_2(slt0_2_out_2));
  // Probe on subtractor_1_out
  // Probe on slt0_1_out_2
  slt0 slt0_3 (.in_1(subtractor_1_out), .out_2(slt0_3_out_2));
  xor xor_1 (xor_1_out, slt0_2_out_2, slt0_1_out_2);
  xor xor_2 (out_3, slt0_3_out_2, xor_1_out);
endmodule

module slt0 (
  input  [31:0] in_1,
  output out_2
);


  assign out_2 = in_1[31];
endmodule

module reverse (
  input  [31:0] in_1,
  output [31:0] out_2
);


  assign out_2 = {in_1[0], in_1[1], in_1[2], in_1[3], in_1[4], in_1[5], in_1[6], in_1[7], in_1[8], in_1[9], in_1[10], in_1[11], in_1[12], in_1[13], in_1[14], in_1[15], in_1[16], in_1[17], in_1[18], in_1[19], in_1[20], in_1[21], in_1[22], in_1[23], in_1[24], in_1[25], in_1[26], in_1[27], in_1[28], in_1[29], in_1[30], in_1[31]};
endmodule
