// Logisim project cpu.circ as structural Verilog: 25 circuits, main circuit main
module main (
  input  [31:0] INSTRUCTION,
  input  CLOCK,
  output [31:0] FETCH_ADDRESS,
  output [31:0] ra,
  output [31:0] sp,
  output [31:0] t0,
  output [31:0] t1,
  output [31:0] t2,
  output [31:0] s0,
  output [31:0] s1,
  output [31:0] a0
);

  wire ASel, BrEq, BrLT, BrUn, BSel, MemRW, not_1_out, PCSel, RegWEn;
  wire [1:0] WBSel;
  wire [2:0] ImmSel;
  wire [3:0] ALUSel;
  wire [31:0] ALUResult, DataA, DataB, DataR, Imm_ans, INSTRUCTION2, multiplexer_1_out, multiplexer_2_out,
       multiplexer_3_out, multiplexer_4_out, PC_add4, PC_D, PC_D_add4, PC_q, WB;

  Adder #(.width(32)) adder_1 (.a(PC_q), .b(32'h4), .out(PC_add4));  // open: cin, cout
  Multiplexer #(.width(32), .enable("false")) multiplexer_1 (
    .in0(PC_add4), .in1(ALUResult), .out(multiplexer_1_out), .sel(PCSel));
  Register #(.width(32)) PC (.D(multiplexer_1_out), .en(1'b1), .clk(CLOCK), .Q(PC_q));  // open: clr
  Shifter #(.width(32), .shift("lr")) shifter_1 (.in(PC_q), .\dist (5'b00010), .out(FETCH_ADDRESS));
  Register #(.width(32)) register_1 (.D(PC_q), .en(1'b1), .clk(CLOCK), .Q(PC_D));  // open: clr
  Controller controller_1 (
    .inst(INSTRUCTION2), .breq(BrEq), .brlt(BrLT), .PCSel(PCSel), .ImmSel(ImmSel), .BrUn(BrUn), .ASel(ASel),
    .BSel(BSel), .ALUSel(ALUSel), .MemRW(MemRW), .RegWEn(RegWEn), .WBSel(WBSel));
  imm_gen imm_gen_1 (.ins(INSTRUCTION2), .immSel(ImmSel), .imm_ans(Imm_ans));
  Adder #(.width(32)) adder_2 (.a(PC_D), .b(32'h4), .out(PC_D_add4));  // open: cin, cout
  regfile_main RegFile (
    .Read_Register_1_rs1(INSTRUCTION2[19:15]), .Read_Register_2_rs2(INSTRUCTION2[24:20]),
    .Write_Register_rd(INSTRUCTION2[11:7]), .Write_Data(WB), .Write_Enable(RegWEn), .Clock(CLOCK),
    .Read_Data_1(DataA), .Read_Data_2(DataB), .ra(ra), .sp(sp), .t0(t0), .t1(t1), .t2(t2), .s0(s0), .s1(s1),
    .a0(a0));
  Multiplexer #(.width(32), .enable("false")) multiplexer_2 (
    .in0(INSTRUCTION), .in1(32'h13), .out(multiplexer_2_out), .sel(PCSel));
  not not_1 (not_1_out, BrUn);
  Multiplexer #(.width(32), .enable("false")) multiplexer_3 (
    .in0(DataA), .in1(PC_D), .out(multiplexer_3_out), .sel(ASel));
  BranchComp branchcomp_1 (.DataA(DataA), .DataB(DataB), .BrUn(not_1_out), .BrEq(BrEq), .BrLT(BrLT));
  Register #(.width(32)) register_2 (.D(multiplexer_2_out), .en(1'b1), .clk(CLOCK), .Q(INSTRUCTION2));  // open: clr
  Multiplexer #(.width(32), .enable("false")) multiplexer_4 (
    .in0(DataB), .in1(Imm_ans), .out(multiplexer_4_out), .sel(BSel));
  Multiplexer #(.select(2), .width(32), .enable("false")) multiplexer_5 (
    .in0(ALUResult), .in1(DataR), .in2(PC_D_add4), .out(WB), .sel(WBSel));  // open: in3
  alu Arithmetic_Logic_Unit (.A(multiplexer_3_out), .B(multiplexer_4_out), .ALUSel(ALUSel), .Result(ALUResult));
  mem_main DMEM (.WriteAddr(ALUResult), .WriteData(DataB), .MemRW(MemRW), .ReadData(DataR), .clk(CLOCK));

  // Other names for the same wires on the sheet: clk = CLOCK; fetch_addr[31:0] = FETCH_ADDRESS

  // Notes on the sheet:
  //   Output
  //   Inputs/Outputs from run.circ. DO NOT MOVE THESE.
  //   Inputs
  //   It is OK to move the PC, RegFile, ALU, and MEM to wherever is most convenient for you when constructing your CPU, and to delete this text
  //   Inputs/Outputs from run.circ. DO NOT MOVE THESE.
endmodule

module Controller (
  input  [31:0] inst,
  input  breq,
  input  brlt,
  output PCSel,
  output [2:0] ImmSel,
  output BrUn,
  output ASel,
  output BSel,
  output [3:0] ALUSel,
  output MemRW,
  output RegWEn,
  output [1:0] WBSel
);

  wire addressdecoder_1_add_flag, addressdecoder_1_addi_flag, addressdecoder_1_and_flag,
       addressdecoder_1_andi_flag, addressdecoder_1_auipc_flag, addressdecoder_1_beq_flag,
       addressdecoder_1_bgeu_flag, addressdecoder_1_blt_flag, addressdecoder_1_bltu_flag,
       addressdecoder_1_bne_flag, addressdecoder_1_div_flag, addressdecoder_1_divu_flag,
       addressdecoder_1_jal_flag, addressdecoder_1_jalr_flag, addressdecoder_1_lb_flag,
       addressdecoder_1_lbu_flag, addressdecoder_1_lh_flag, addressdecoder_1_lhu_flag,
       addressdecoder_1_lui_flag, addressdecoder_1_lw_flag, addressdecoder_1_mul_flag,
       addressdecoder_1_mulh_flag, addressdecoder_1_mulhu_flag, addressdecoder_1_or_flag,
       addressdecoder_1_ori_flag, addressdecoder_1_remu_flag, addressdecoder_1_sll_flag,
       addressdecoder_1_slli_flag, addressdecoder_1_slti_flag, addressdecoder_1_srl_flag,
       addressdecoder_1_srli_flag, addressdecoder_1_sub_flag, addressdecoder_1_sw_flag,
       addressdecoder_1_xor_flag, addressdecoder_1_xori_flag;

  AddressDecoder addressdecoder_1 (
    .inst(inst), .add_flag(addressdecoder_1_add_flag), .mul_flag(addressdecoder_1_mul_flag),
    .sub_flag(addressdecoder_1_sub_flag), .sll_flag(addressdecoder_1_sll_flag),
    .mulh_flag(addressdecoder_1_mulh_flag), .mulhu_flag(addressdecoder_1_mulhu_flag),
    .xor_flag(addressdecoder_1_xor_flag), .div_flag(addressdecoder_1_div_flag),
    .divu_flag(addressdecoder_1_divu_flag), .srl_flag(addressdecoder_1_srl_flag),
    .or_flag(addressdecoder_1_or_flag), .remu_flag(addressdecoder_1_remu_flag),
    .and_flag(addressdecoder_1_and_flag), .lb_flag(addressdecoder_1_lb_flag),
    .lh_flag(addressdecoder_1_lh_flag), .lw_flag(addressdecoder_1_lw_flag),
    .lbu_flag(addressdecoder_1_lbu_flag), .lhu_flag(addressdecoder_1_lhu_flag),
    .addi_flag(addressdecoder_1_addi_flag), .slli_flag(addressdecoder_1_slli_flag),
    .slti_flag(addressdecoder_1_slti_flag), .xori_flag(addressdecoder_1_xori_flag),
    .srli_flag(addressdecoder_1_srli_flag), .ori_flag(addressdecoder_1_ori_flag),
    .andi_flag(addressdecoder_1_andi_flag), .sw_flag(addressdecoder_1_sw_flag),
    .beq_flag(addressdecoder_1_beq_flag), .blt_flag(addressdecoder_1_blt_flag),
    .bltu_flag(addressdecoder_1_bltu_flag), .bne_flag(addressdecoder_1_bne_flag),
    .bgeu_flag(addressdecoder_1_bgeu_flag), .auipc_flag(addressdecoder_1_auipc_flag),
    .lui_flag(addressdecoder_1_lui_flag), .jal_flag(addressdecoder_1_jal_flag),
    .jalr_flag(addressdecoder_1_jalr_flag));
  // AND_Gate and_1 is placed but not wired
  ControllerOutput controlleroutput_1 (
    .add_flag(addressdecoder_1_add_flag), .mul_flag(addressdecoder_1_mul_flag),
    .sub_flag(addressdecoder_1_sub_flag), .sll_flag(addressdecoder_1_sll_flag),
    .mulh_flag(addressdecoder_1_mulh_flag), .mulhu_flag(addressdecoder_1_mulhu_flag),
    .xor_flag(addressdecoder_1_xor_flag), .div_flag(addressdecoder_1_div_flag),
    .divu_flag(addressdecoder_1_divu_flag), .srl_flag(addressdecoder_1_srl_flag),
    .or_flag(addressdecoder_1_or_flag), .remu_flag(addressdecoder_1_remu_flag),
    .and_flag(addressdecoder_1_and_flag), .lb_flag(addressdecoder_1_lb_flag),
    .lh_flag(addressdecoder_1_lh_flag), .lw_flag(addressdecoder_1_lw_flag),
    .lbu_flag(addressdecoder_1_lbu_flag), .lhu_flag(addressdecoder_1_lhu_flag),
    .addi_flag(addressdecoder_1_addi_flag), .slli_flag(addressdecoder_1_slli_flag),
    .slti_flag(addressdecoder_1_slti_flag), .xori_flag(addressdecoder_1_xori_flag),
    .srli_flag(addressdecoder_1_srli_flag), .ori_flag(addressdecoder_1_ori_flag),
    .andi_flag(addressdecoder_1_andi_flag), .sw_flag(addressdecoder_1_sw_flag),
    .beq_flag(addressdecoder_1_beq_flag), .blt_flag(addressdecoder_1_blt_flag),
    .bltu_flag(addressdecoder_1_bltu_flag), .bne_flag(addressdecoder_1_bne_flag),
    .bgeu_flag(addressdecoder_1_bgeu_flag), .auipc_flag(addressdecoder_1_auipc_flag),
    .lui_flag(addressdecoder_1_lui_flag), .jal_flag(addressdecoder_1_jal_flag),
    .jalr_flag(addressdecoder_1_jalr_flag), .breq_flag(breq), .brlt_flag(brlt), .PCSelOutput(PCSel),
    .ImmSelOutput(ImmSel), .BrUnOutput(BrUn), .ASelOutput(ASel), .BSelOutput(BSel), .ALUSelOutput(ALUSel),
    .MemRWOutput(MemRW), .RegWEnOutput(RegWEn), .WBSelOutput(WBSel));
endmodule

module AddressDecoder (
  input  [31:0] inst,
  output add_flag,
  output mul_flag,
  output sub_flag,
  output sll_flag,
  output mulh_flag,
  output mulhu_flag,
  output xor_flag,
  output div_flag,
  output divu_flag,
  output srl_flag,
  output or_flag,
  output remu_flag,
  output and_flag,
  output lb_flag,
  output lh_flag,
  output lw_flag,
  output lbu_flag,
  output lhu_flag,
  output addi_flag,
  output slli_flag,
  output slti_flag,
  output xori_flag,
  output srli_flag,
  output ori_flag,
  output andi_flag,
  output sw_flag,
  output beq_flag,
  output blt_flag,
  output bltu_flag,
  output bne_flag,
  output bgeu_flag,
  output auipc_flag,
  output lui_flag,
  output jal_flag,
  output jalr_flag
);

  wire not_1_out, not_2_out, not_3_out, not_4_out, not_5_out, not_6_out, not_7_out, not_8_out, not_9_out,
       not_10_out, not_11_out, not_12_out, not_13_out, not_14_out, not_15_out, not_16_out, not_17_out,
       not_18_out, not_19_out, not_20_out, not_21_out, not_22_out, not_23_out, not_24_out, not_25_out,
       not_26_out, not_27_out, not_28_out, not_29_out, not_30_out, not_31_out, not_32_out, not_33_out,
       not_34_out, not_35_out, not_36_out, not_37_out, not_38_out, not_39_out, not_40_out, not_41_out,
       not_42_out, not_43_out, not_44_out, not_45_out, not_46_out, not_47_out, not_48_out, not_49_out,
       not_50_out, not_51_out, not_52_out, not_53_out, not_54_out, not_55_out, not_56_out, not_57_out,
       not_58_out, not_59_out, not_60_out, not_61_out, not_62_out, not_63_out, not_64_out, not_65_out,
       not_66_out, not_67_out, not_68_out, not_69_out, not_70_out, not_71_out, not_72_out, not_73_out,
       not_74_out, not_75_out, not_76_out, not_77_out, not_78_out, not_79_out, not_80_out, not_81_out,
       not_82_out, not_83_out, not_84_out, not_85_out, not_86_out, not_87_out, not_88_out, not_89_out,
       not_90_out, not_91_out, not_92_out, not_93_out, not_94_out, not_95_out, not_96_out, not_97_out,
       not_98_out, not_99_out, not_100_out, not_101_out, not_102_out, not_103_out, not_104_out, not_105_out,
       not_106_out, not_107_out, not_108_out, not_109_out, not_110_out, not_111_out, not_112_out,
       not_113_out, not_114_out, not_115_out, not_116_out, not_117_out, not_118_out, not_119_out,
       not_120_out, not_121_out, not_122_out, not_123_out, not_124_out, not_125_out, not_126_out,
       not_127_out, not_128_out, not_129_out, not_130_out, not_131_out, not_132_out, not_133_out,
       not_134_out, not_135_out, not_136_out, not_137_out, not_138_out, not_139_out, not_140_out,
       not_141_out, not_142_out, not_143_out, not_144_out, not_145_out, not_146_out, not_147_out,
       not_148_out, not_149_out, not_150_out, not_151_out, not_152_out, not_153_out, not_154_out,
       not_155_out, not_156_out, not_157_out, not_158_out, not_159_out, not_160_out, not_161_out,
       not_162_out, not_163_out, not_164_out, not_165_out, not_166_out, not_167_out, not_168_out,
       not_169_out, not_170_out, not_171_out, not_172_out, not_173_out, not_174_out, not_175_out,
       not_176_out, not_177_out, not_178_out, not_179_out, not_180_out, not_181_out, not_182_out,
       not_183_out, not_184_out, not_185_out, not_186_out, not_187_out, not_188_out, not_189_out,
       not_190_out, not_191_out, not_192_out, not_193_out, not_194_out, not_195_out, not_196_out,
       not_197_out, not_198_out, not_199_out, not_200_out, not_201_out, not_202_out, not_203_out,
       not_204_out, not_205_out, not_206_out, not_207_out, not_208_out, not_209_out, not_210_out,
       not_211_out, not_212_out, not_213_out, not_214_out, not_215_out, not_216_out, not_217_out,
       not_218_out, not_219_out, not_220_out, not_221_out, not_222_out, not_223_out, not_224_out,
       not_225_out, not_226_out, not_227_out, not_228_out, not_229_out, not_230_out, not_231_out,
       not_232_out, not_233_out, not_234_out, not_235_out, not_236_out, not_237_out, not_238_out,
       not_239_out, not_240_out, not_241_out, not_242_out, not_243_out, not_244_out, not_245_out,
       not_246_out, not_247_out, not_248_out, not_249_out, not_250_out, not_251_out, not_252_out,
       not_253_out, not_254_out, not_255_out, not_256_out, not_257_out, not_258_out, not_259_out,
       not_260_out, not_261_out, not_262_out, not_263_out, not_264_out, not_265_out, not_266_out,
       not_267_out, not_268_out, not_269_out, not_270_out, not_271_out, not_272_out, or_1_out, or_2_out,
       or_3_out, or_4_out, or_5_out, or_6_out, or_7_out, or_8_out, or_9_out, or_10_out, or_11_out, or_12_out,
       or_13_out, or_14_out, or_15_out, or_16_out, or_17_out, or_18_out, or_19_out, or_20_out, or_21_out,
       or_22_out, or_23_out, or_24_out, or_25_out, or_26_out, or_27_out, or_28_out, or_29_out, or_30_out,
       or_31_out, or_32_out, or_33_out, or_34_out, or_35_out, or_36_out, or_37_out, or_38_out, or_39_out,
       or_40_out, or_41_out, or_42_out, or_43_out, or_44_out, or_45_out, or_46_out, or_47_out, or_48_out,
       or_49_out, or_50_out, or_51_out, or_52_out, or_53_out, or_54_out, or_55_out, or_56_out, or_57_out,
       or_58_out, or_59_out, or_60_out, or_61_out, or_62_out, or_63_out, or_64_out, or_65_out, or_66_out,
       or_67_out, or_68_out, or_69_out, or_70_out, or_71_out, or_72_out, or_73_out, or_74_out, or_75_out,
       or_76_out, or_77_out, or_78_out, or_79_out, or_80_out, or_81_out, or_82_out, or_83_out, or_84_out,
       or_85_out, or_86_out, or_87_out, or_88_out, or_89_out, or_90_out, or_91_out, or_92_out, or_93_out,
       or_94_out, or_95_out, or_96_out, or_97_out, or_98_out, or_99_out, or_100_out, or_101_out, or_102_out,
       or_103_out, or_104_out, or_105_out, or_106_out, or_107_out, or_108_out, or_109_out, or_110_out,
       or_111_out, or_112_out, or_113_out, or_114_out, or_115_out, or_116_out, or_117_out, or_118_out,
       or_119_out, or_120_out, or_121_out, or_122_out, or_123_out, or_124_out, or_125_out, or_126_out,
       or_127_out, or_128_out, or_129_out, or_130_out, or_131_out, or_132_out, or_133_out, or_134_out,
       or_135_out, or_136_out, or_137_out, or_138_out, or_139_out, or_140_out, or_141_out, or_142_out,
       or_143_out, or_144_out, or_145_out, or_146_out, or_147_out, or_148_out, or_149_out, or_150_out,
       or_151_out, or_152_out, or_153_out, or_154_out, or_155_out, or_156_out, or_157_out, or_158_out,
       or_159_out, or_160_out, or_161_out, or_162_out, or_163_out, or_164_out, or_165_out, or_166_out,
       or_167_out, or_168_out, or_169_out, or_170_out, or_171_out, or_172_out, or_173_out, or_174_out,
       or_175_out, or_176_out, or_177_out, or_178_out, or_179_out, or_180_out, or_181_out, or_182_out,
       or_183_out, or_184_out, or_185_out, or_186_out, or_187_out, or_188_out, or_189_out, or_190_out,
       or_191_out, or_192_out, or_193_out, or_194_out, or_195_out, or_196_out, or_197_out, or_198_out,
       or_199_out, or_200_out, or_201_out, or_202_out, or_203_out, or_204_out, or_205_out, or_206_out,
       or_207_out, or_208_out, or_209_out, or_210_out, or_211_out, or_212_out, or_213_out, or_214_out,
       or_215_out, or_216_out, or_217_out, or_218_out, or_219_out, or_220_out, or_221_out, or_222_out,
       or_223_out, or_224_out, or_225_out, or_226_out, or_227_out, or_228_out, or_229_out, or_230_out,
       or_231_out, or_232_out, or_233_out, or_234_out, or_235_out, or_236_out, or_237_out, or_238_out,
       or_239_out, or_240_out, or_241_out, or_242_out, or_243_out, or_244_out, or_245_out, or_246_out,
       or_247_out, or_248_out, or_249_out, or_250_out, or_251_out, or_252_out, or_253_out, or_254_out,
       or_255_out, or_256_out, or_257_out, or_258_out, or_259_out, or_260_out, or_261_out, or_262_out,
       or_263_out, or_264_out, or_265_out, or_266_out, or_267_out, or_268_out, or_269_out, or_270_out,
       or_271_out, or_272_out, or_273_out, or_274_out, or_275_out, or_276_out, or_277_out, or_278_out,
       or_279_out, or_280_out, or_281_out, or_282_out, or_283_out, or_284_out, or_285_out, or_286_out,
       or_287_out, or_288_out, or_289_out, or_290_out, or_291_out, or_292_out, or_293_out, or_294_out,
       or_295_out, or_296_out, or_297_out, or_298_out, or_299_out, or_300_out, or_301_out, or_302_out,
       or_303_out, or_304_out, or_305_out, or_306_out, or_307_out, or_308_out, or_309_out, or_310_out,
       or_311_out, or_312_out, or_313_out, or_314_out, or_315_out, or_316_out, or_317_out, or_318_out,
       or_319_out, or_320_out, or_321_out, or_322_out, or_323_out, or_324_out, or_325_out, or_326_out,
       or_327_out, or_328_out, or_329_out, or_330_out, or_331_out, or_332_out, or_333_out, or_334_out,
       or_335_out, or_336_out, or_337_out, or_338_out, or_339_out, or_340_out, or_341_out, or_342_out,
       or_343_out, or_344_out, or_345_out, or_346_out, or_347_out, or_348_out, or_349_out, or_350_out,
       or_351_out, or_352_out, or_353_out, or_354_out, or_355_out, or_356_out, or_357_out, or_358_out,
       or_359_out, or_360_out, or_361_out, or_362_out, or_363_out, or_364_out, or_365_out, or_366_out,
       or_367_out, or_368_out, or_369_out, or_370_out, or_371_out, or_372_out, or_373_out, or_374_out,
       or_375_out, or_376_out, or_377_out, or_378_out, or_379_out, or_380_out, or_381_out, or_382_out,
       or_383_out, or_384_out, or_385_out, or_386_out, or_387_out, or_388_out, or_389_out, or_390_out,
       or_391_out, or_392_out, or_393_out, or_394_out, or_395_out, or_396_out, or_397_out, or_398_out,
       or_399_out, or_400_out, or_401_out, or_402_out, or_403_out, or_404_out, or_405_out, or_406_out,
       or_407_out, or_408_out, or_409_out, or_410_out, or_411_out, or_412_out, or_413_out, or_414_out,
       or_415_out, or_416_out, or_417_out, or_418_out, or_419_out, or_420_out, or_421_out, or_422_out,
       or_423_out, or_424_out, or_425_out, or_426_out, or_427_out, or_428_out, or_429_out, or_430_out,
       or_431_out, or_432_out, or_433_out, or_434_out, or_435_out, or_436_out, or_437_out, or_438_out,
       or_439_out, or_440_out, or_441_out, or_442_out, or_443_out, or_444_out, or_445_out, or_446_out,
       or_447_out, or_448_out, or_449_out, or_450_out, or_451_out, or_452_out, or_453_out, or_454_out,
       or_455_out, or_456_out, or_457_out, or_458_out, or_459_out, or_460_out, or_461_out, or_462_out,
       or_463_out, or_464_out, or_465_out, or_466_out, or_467_out, or_468_out, or_469_out, or_470_out,
       or_471_out, or_472_out, or_473_out, or_474_out, or_475_out, or_476_out, or_477_out, or_478_out,
       or_479_out, or_480_out, or_481_out, or_482_out, or_483_out, or_484_out, or_485_out, or_486_out,
       or_487_out, or_488_out, or_489_out, or_490_out, or_491_out, or_492_out, or_493_out, or_494_out,
       or_495_out, or_496_out, or_497_out, or_498_out, or_499_out, or_500_out, or_501_out, or_502_out,
       or_503_out, or_504_out, or_505_out, or_506_out, or_507_out, or_508_out, or_509_out, or_510_out,
       or_511_out, or_512_out, or_513_out, or_514_out, or_515_out, or_516_out, or_517_out, or_518_out,
       or_519_out, or_520_out, or_521_out, or_522_out, or_523_out, or_524_out, or_525_out;

  not not_1 (not_1_out, inst[2]);
  not not_2 (not_2_out, inst[3]);
  not not_3 (not_3_out, inst[6]);
  not not_4 (not_4_out, inst[12]);
  not not_5 (not_5_out, inst[13]);
  not not_6 (not_6_out, inst[14]);
  not not_7 (not_7_out, inst[25]);
  not not_8 (not_8_out, inst[26]);
  not not_9 (not_9_out, inst[27]);
  not not_10 (not_10_out, inst[28]);
  not not_11 (not_11_out, inst[29]);
  not not_12 (not_12_out, inst[30]);
  not not_13 (not_13_out, inst[31]);
  not not_14 (not_14_out, inst[2]);
  not not_15 (not_15_out, inst[3]);
  not not_16 (not_16_out, inst[6]);
  not not_17 (not_17_out, inst[12]);
  not not_18 (not_18_out, inst[13]);
  not not_19 (not_19_out, inst[14]);
  not not_20 (not_20_out, inst[26]);
  not not_21 (not_21_out, inst[27]);
  not not_22 (not_22_out, inst[28]);
  not not_23 (not_23_out, inst[29]);
  not not_24 (not_24_out, inst[30]);
  not not_25 (not_25_out, inst[31]);
  not not_26 (not_26_out, inst[2]);
  not not_27 (not_27_out, inst[3]);
  not not_28 (not_28_out, inst[6]);
  not not_29 (not_29_out, inst[12]);
  not not_30 (not_30_out, inst[13]);
  not not_31 (not_31_out, inst[14]);
  not not_32 (not_32_out, inst[25]);
  not not_33 (not_33_out, inst[26]);
  not not_34 (not_34_out, inst[27]);
  not not_35 (not_35_out, inst[28]);
  not not_36 (not_36_out, inst[29]);
  not not_37 (not_37_out, inst[31]);
  not not_38 (not_38_out, inst[2]);
  not not_39 (not_39_out, inst[3]);
  not not_40 (not_40_out, inst[6]);
  not not_41 (not_41_out, inst[13]);
  not not_42 (not_42_out, inst[14]);
  not not_43 (not_43_out, inst[25]);
  not not_44 (not_44_out, inst[26]);
  not not_45 (not_45_out, inst[27]);
  not not_46 (not_46_out, inst[28]);
  not not_47 (not_47_out, inst[29]);
  not not_48 (not_48_out, inst[30]);
  not not_49 (not_49_out, inst[31]);
  not not_50 (not_50_out, inst[2]);
  not not_51 (not_51_out, inst[3]);
  not not_52 (not_52_out, inst[6]);
  not not_53 (not_53_out, inst[13]);
  not not_54 (not_54_out, inst[14]);
  not not_55 (not_55_out, inst[26]);
  not not_56 (not_56_out, inst[27]);
  not not_57 (not_57_out, inst[28]);
  not not_58 (not_58_out, inst[29]);
  not not_59 (not_59_out, inst[30]);
  not not_60 (not_60_out, inst[31]);
  not not_61 (not_61_out, inst[2]);
  not not_62 (not_62_out, inst[3]);
  not not_63 (not_63_out, inst[6]);
  not not_64 (not_64_out, inst[14]);
  not not_65 (not_65_out, inst[26]);
  not not_66 (not_66_out, inst[27]);
  not not_67 (not_67_out, inst[28]);
  not not_68 (not_68_out, inst[29]);
  not not_69 (not_69_out, inst[30]);
  not not_70 (not_70_out, inst[31]);
  not not_71 (not_71_out, inst[2]);
  not not_72 (not_72_out, inst[3]);
  not not_73 (not_73_out, inst[6]);
  not not_74 (not_74_out, inst[12]);
  not not_75 (not_75_out, inst[13]);
  not not_76 (not_76_out, inst[25]);
  not not_77 (not_77_out, inst[26]);
  not not_78 (not_78_out, inst[27]);
  not not_79 (not_79_out, inst[28]);
  not not_80 (not_80_out, inst[29]);
  not not_81 (not_81_out, inst[30]);
  not not_82 (not_82_out, inst[31]);
  not not_83 (not_83_out, inst[2]);
  not not_84 (not_84_out, inst[3]);
  not not_85 (not_85_out, inst[6]);
  not not_86 (not_86_out, inst[12]);
  not not_87 (not_87_out, inst[13]);
  not not_88 (not_88_out, inst[26]);
  not not_89 (not_89_out, inst[27]);
  not not_90 (not_90_out, inst[28]);
  not not_91 (not_91_out, inst[29]);
  not not_92 (not_92_out, inst[30]);
  not not_93 (not_93_out, inst[31]);
  not not_94 (not_94_out, inst[2]);
  not not_95 (not_95_out, inst[3]);
  not not_96 (not_96_out, inst[6]);
  not not_97 (not_97_out, inst[13]);
  not not_98 (not_98_out, inst[26]);
  not not_99 (not_99_out, inst[27]);
  not not_100 (not_100_out, inst[28]);
  not not_101 (not_101_out, inst[29]);
  not not_102 (not_102_out, inst[30]);
  not not_103 (not_103_out, inst[31]);
  not not_104 (not_104_out, inst[2]);
  not not_105 (not_105_out, inst[3]);
  not not_106 (not_106_out, inst[6]);
  not not_107 (not_107_out, inst[13]);
  not not_108 (not_108_out, inst[25]);
  not not_109 (not_109_out, inst[26]);
  not not_110 (not_110_out, inst[27]);
  not not_111 (not_111_out, inst[28]);
  not not_112 (not_112_out, inst[29]);
  not not_113 (not_113_out, inst[30]);
  not not_114 (not_114_out, inst[31]);
  not not_115 (not_115_out, inst[2]);
  not not_116 (not_116_out, inst[3]);
  not not_117 (not_117_out, inst[6]);
  not not_118 (not_118_out, inst[12]);
  not not_119 (not_119_out, inst[25]);
  not not_120 (not_120_out, inst[26]);
  not not_121 (not_121_out, inst[27]);
  not not_122 (not_122_out, inst[28]);
  not not_123 (not_123_out, inst[29]);
  not not_124 (not_124_out, inst[30]);
  not not_125 (not_125_out, inst[31]);
  not not_126 (not_126_out, inst[2]);
  not not_127 (not_127_out, inst[3]);
  not not_128 (not_128_out, inst[6]);
  not not_129 (not_129_out, inst[26]);
  not not_130 (not_130_out, inst[27]);
  not not_131 (not_131_out, inst[28]);
  not not_132 (not_132_out, inst[29]);
  not not_133 (not_133_out, inst[30]);
  not not_134 (not_134_out, inst[31]);
  not not_135 (not_135_out, inst[2]);
  not not_136 (not_136_out, inst[3]);
  not not_137 (not_137_out, inst[6]);
  not not_138 (not_138_out, inst[25]);
  not not_139 (not_139_out, inst[26]);
  not not_140 (not_140_out, inst[27]);
  not not_141 (not_141_out, inst[28]);
  not not_142 (not_142_out, inst[29]);
  not not_143 (not_143_out, inst[30]);
  not not_144 (not_144_out, inst[31]);
  not not_145 (not_145_out, inst[2]);
  not not_146 (not_146_out, inst[3]);
  not not_147 (not_147_out, inst[4]);
  not not_148 (not_148_out, inst[5]);
  not not_149 (not_149_out, inst[6]);
  not not_150 (not_150_out, inst[12]);
  not not_151 (not_151_out, inst[13]);
  not not_152 (not_152_out, inst[14]);
  not not_153 (not_153_out, inst[2]);
  not not_154 (not_154_out, inst[3]);
  not not_155 (not_155_out, inst[4]);
  not not_156 (not_156_out, inst[5]);
  not not_157 (not_157_out, inst[6]);
  not not_158 (not_158_out, inst[13]);
  not not_159 (not_159_out, inst[14]);
  not not_160 (not_160_out, inst[2]);
  not not_161 (not_161_out, inst[3]);
  not not_162 (not_162_out, inst[4]);
  not not_163 (not_163_out, inst[5]);
  not not_164 (not_164_out, inst[6]);
  not not_165 (not_165_out, inst[12]);
  not not_166 (not_166_out, inst[14]);
  not not_167 (not_167_out, inst[2]);
  not not_168 (not_168_out, inst[3]);
  not not_169 (not_169_out, inst[4]);
  not not_170 (not_170_out, inst[5]);
  not not_171 (not_171_out, inst[6]);
  not not_172 (not_172_out, inst[12]);
  not not_173 (not_173_out, inst[13]);
  not not_174 (not_174_out, inst[2]);
  not not_175 (not_175_out, inst[3]);
  not not_176 (not_176_out, inst[4]);
  not not_177 (not_177_out, inst[5]);
  not not_178 (not_178_out, inst[6]);
  not not_179 (not_179_out, inst[13]);
  not not_180 (not_180_out, inst[2]);
  not not_181 (not_181_out, inst[3]);
  not not_182 (not_182_out, inst[5]);
  not not_183 (not_183_out, inst[6]);
  not not_184 (not_184_out, inst[12]);
  not not_185 (not_185_out, inst[13]);
  not not_186 (not_186_out, inst[14]);
  not not_187 (not_187_out, inst[2]);
  not not_188 (not_188_out, inst[3]);
  not not_189 (not_189_out, inst[5]);
  not not_190 (not_190_out, inst[6]);
  not not_191 (not_191_out, inst[13]);
  not not_192 (not_192_out, inst[14]);
  not not_193 (not_193_out, inst[25]);
  not not_194 (not_194_out, inst[26]);
  not not_195 (not_195_out, inst[27]);
  not not_196 (not_196_out, inst[28]);
  not not_197 (not_197_out, inst[29]);
  not not_198 (not_198_out, inst[30]);
  not not_199 (not_199_out, inst[31]);
  not not_200 (not_200_out, inst[2]);
  not not_201 (not_201_out, inst[3]);
  not not_202 (not_202_out, inst[5]);
  not not_203 (not_203_out, inst[6]);
  not not_204 (not_204_out, inst[12]);
  not not_205 (not_205_out, inst[14]);
  not not_206 (not_206_out, inst[2]);
  not not_207 (not_207_out, inst[3]);
  not not_208 (not_208_out, inst[5]);
  not not_209 (not_209_out, inst[6]);
  not not_210 (not_210_out, inst[12]);
  not not_211 (not_211_out, inst[13]);
  not not_212 (not_212_out, inst[2]);
  not not_213 (not_213_out, inst[3]);
  not not_214 (not_214_out, inst[5]);
  not not_215 (not_215_out, inst[6]);
  not not_216 (not_216_out, inst[13]);
  not not_217 (not_217_out, inst[25]);
  not not_218 (not_218_out, inst[26]);
  not not_219 (not_219_out, inst[27]);
  not not_220 (not_220_out, inst[28]);
  not not_221 (not_221_out, inst[29]);
  not not_222 (not_222_out, inst[30]);
  not not_223 (not_223_out, inst[31]);
  not not_224 (not_224_out, inst[2]);
  not not_225 (not_225_out, inst[3]);
  not not_226 (not_226_out, inst[5]);
  not not_227 (not_227_out, inst[6]);
  not not_228 (not_228_out, inst[12]);
  not not_229 (not_229_out, inst[2]);
  not not_230 (not_230_out, inst[3]);
  not not_231 (not_231_out, inst[5]);
  not not_232 (not_232_out, inst[6]);
  not not_233 (not_233_out, inst[2]);
  not not_234 (not_234_out, inst[3]);
  not not_235 (not_235_out, inst[4]);
  not not_236 (not_236_out, inst[6]);
  not not_237 (not_237_out, inst[12]);
  not not_238 (not_238_out, inst[14]);
  not not_239 (not_239_out, inst[2]);
  not not_240 (not_240_out, inst[3]);
  not not_241 (not_241_out, inst[4]);
  not not_242 (not_242_out, inst[12]);
  not not_243 (not_243_out, inst[13]);
  not not_244 (not_244_out, inst[14]);
  not not_245 (not_245_out, inst[2]);
  not not_246 (not_246_out, inst[3]);
  not not_247 (not_247_out, inst[4]);
  not not_248 (not_248_out, inst[12]);
  not not_249 (not_249_out, inst[13]);
  not not_250 (not_250_out, inst[2]);
  not not_251 (not_251_out, inst[3]);
  not not_252 (not_252_out, inst[4]);
  not not_253 (not_253_out, inst[12]);
  not not_254 (not_254_out, inst[2]);
  not not_255 (not_255_out, inst[3]);
  not not_256 (not_256_out, inst[4]);
  not not_257 (not_257_out, inst[13]);
  not not_258 (not_258_out, inst[14]);
  not not_259 (not_259_out, inst[2]);
  not not_260 (not_260_out, inst[3]);
  not not_261 (not_261_out, inst[4]);
  not not_262 (not_262_out, inst[3]);
  not not_263 (not_263_out, inst[5]);
  not not_264 (not_264_out, inst[6]);
  not not_265 (not_265_out, inst[3]);
  not not_266 (not_266_out, inst[6]);
  not not_267 (not_267_out, inst[4]);
  not not_268 (not_268_out, inst[3]);
  not not_269 (not_269_out, inst[4]);
  not not_270 (not_270_out, inst[12]);
  not not_271 (not_271_out, inst[13]);
  not not_272 (not_272_out, inst[14]);
  or or_1 (or_1_out, not_1_out, 1'b0);
  or or_2 (or_2_out, not_2_out, 1'b0);
  or or_3 (or_3_out, inst[4], 1'b0);
  or or_4 (or_4_out, inst[5], 1'b0);
  or or_5 (or_5_out, not_3_out, 1'b0);
  or or_6 (or_6_out, not_4_out, 1'b0);
  or or_7 (or_7_out, not_5_out, 1'b0);
  or or_8 (or_8_out, not_6_out, 1'b0);
  or or_9 (or_9_out, not_7_out, 1'b0);
  or or_10 (or_10_out, not_8_out, 1'b0);
  or or_11 (or_11_out, not_9_out, 1'b0);
  or or_12 (or_12_out, not_10_out, 1'b0);
  or or_13 (or_13_out, not_11_out, 1'b0);
  or or_14 (or_14_out, not_12_out, 1'b0);
  or or_15 (or_15_out, not_13_out, 1'b0);
  or or_16 (or_16_out, not_14_out, 1'b0);
  or or_17 (or_17_out, not_15_out, 1'b0);
  or or_18 (or_18_out, inst[4], 1'b0);
  or or_19 (or_19_out, inst[5], 1'b0);
  or or_20 (or_20_out, not_16_out, 1'b0);
  or or_21 (or_21_out, not_17_out, 1'b0);
  or or_22 (or_22_out, not_18_out, 1'b0);
  or or_23 (or_23_out, not_19_out, 1'b0);
  or or_24 (or_24_out, inst[25], 1'b0);
  or or_25 (or_25_out, not_20_out, 1'b0);
  or or_26 (or_26_out, not_21_out, 1'b0);
  or or_27 (or_27_out, not_22_out, 1'b0);
  or or_28 (or_28_out, not_23_out, 1'b0);
  or or_29 (or_29_out, not_24_out, 1'b0);
  or or_30 (or_30_out, not_25_out, 1'b0);
  or or_31 (or_31_out, not_26_out, 1'b0);
  or or_32 (or_32_out, not_27_out, 1'b0);
  or or_33 (or_33_out, inst[4], 1'b0);
  or or_34 (or_34_out, inst[5], 1'b0);
  or or_35 (or_35_out, not_28_out, 1'b0);
  or or_36 (or_36_out, not_29_out, 1'b0);
  or or_37 (or_37_out, not_30_out, 1'b0);
  or or_38 (or_38_out, not_31_out, 1'b0);
  or or_39 (or_39_out, not_32_out, 1'b0);
  or or_40 (or_40_out, not_33_out, 1'b0);
  or or_41 (or_41_out, not_34_out, 1'b0);
  or or_42 (or_42_out, not_35_out, 1'b0);
  or or_43 (or_43_out, not_36_out, 1'b0);
  or or_44 (or_44_out, inst[30], 1'b0);
  or or_45 (or_45_out, not_37_out, 1'b0);
  or or_46 (or_46_out, not_38_out, 1'b0);
  or or_47 (or_47_out, not_39_out, 1'b0);
  or or_48 (or_48_out, inst[4], 1'b0);
  or or_49 (or_49_out, inst[5], 1'b0);
  or or_50 (or_50_out, not_40_out, 1'b0);
  or or_51 (or_51_out, inst[12], 1'b0);
  or or_52 (or_52_out, not_41_out, 1'b0);
  or or_53 (or_53_out, not_42_out, 1'b0);
  or or_54 (or_54_out, not_43_out, 1'b0);
  or or_55 (or_55_out, not_44_out, 1'b0);
  or or_56 (or_56_out, not_45_out, 1'b0);
  or or_57 (or_57_out, not_46_out, 1'b0);
  or or_58 (or_58_out, not_47_out, 1'b0);
  or or_59 (or_59_out, not_48_out, 1'b0);
  or or_60 (or_60_out, not_49_out, 1'b0);
  or or_61 (or_61_out, not_50_out, 1'b0);
  or or_62 (or_62_out, not_51_out, 1'b0);
  or or_63 (or_63_out, inst[4], 1'b0);
  or or_64 (or_64_out, inst[5], 1'b0);
  or or_65 (or_65_out, not_52_out, 1'b0);
  or or_66 (or_66_out, inst[12], 1'b0);
  or or_67 (or_67_out, not_53_out, 1'b0);
  or or_68 (or_68_out, not_54_out, 1'b0);
  or or_69 (or_69_out, inst[25], 1'b0);
  or or_70 (or_70_out, not_55_out, 1'b0);
  or or_71 (or_71_out, not_56_out, 1'b0);
  or or_72 (or_72_out, not_57_out, 1'b0);
  or or_73 (or_73_out, not_58_out, 1'b0);
  or or_74 (or_74_out, not_59_out, 1'b0);
  or or_75 (or_75_out, not_60_out, 1'b0);
  or or_76 (or_76_out, not_61_out, 1'b0);
  or or_77 (or_77_out, not_62_out, 1'b0);
  or or_78 (or_78_out, inst[4], 1'b0);
  or or_79 (or_79_out, inst[5], 1'b0);
  or or_80 (or_80_out, not_63_out, 1'b0);
  or or_81 (or_81_out, inst[12], 1'b0);
  or or_82 (or_82_out, inst[13], 1'b0);
  or or_83 (or_83_out, not_64_out, 1'b0);
  or or_84 (or_84_out, inst[25], 1'b0);
  or or_85 (or_85_out, not_65_out, 1'b0);
  or or_86 (or_86_out, not_66_out, 1'b0);
  or or_87 (or_87_out, not_67_out, 1'b0);
  or or_88 (or_88_out, not_68_out, 1'b0);
  or or_89 (or_89_out, not_69_out, 1'b0);
  or or_90 (or_90_out, not_70_out, 1'b0);
  or or_91 (or_91_out, not_71_out, 1'b0);
  or or_92 (or_92_out, not_72_out, 1'b0);
  or or_93 (or_93_out, inst[4], 1'b0);
  or or_94 (or_94_out, inst[5], 1'b0);
  or or_95 (or_95_out, not_73_out, 1'b0);
  or or_96 (or_96_out, not_74_out, 1'b0);
  or or_97 (or_97_out, not_75_out, 1'b0);
  or or_98 (or_98_out, inst[14], 1'b0);
  or or_99 (or_99_out, not_76_out, 1'b0);
  or or_100 (or_100_out, not_77_out, 1'b0);
  or or_101 (or_101_out, not_78_out, 1'b0);
  or or_102 (or_102_out, not_79_out, 1'b0);
  or or_103 (or_103_out, not_80_out, 1'b0);
  or or_104 (or_104_out, not_81_out, 1'b0);
  or or_105 (or_105_out, not_82_out, 1'b0);
  or or_106 (or_106_out, not_83_out, 1'b0);
  or or_107 (or_107_out, not_84_out, 1'b0);
  or or_108 (or_108_out, inst[4], 1'b0);
  or or_109 (or_109_out, inst[5], 1'b0);
  or or_110 (or_110_out, not_85_out, 1'b0);
  or or_111 (or_111_out, not_86_out, 1'b0);
  or or_112 (or_112_out, not_87_out, 1'b0);
  or or_113 (or_113_out, inst[14], 1'b0);
  or or_114 (or_114_out, inst[25], 1'b0);
  or or_115 (or_115_out, not_88_out, 1'b0);
  or or_116 (or_116_out, not_89_out, 1'b0);
  or or_117 (or_117_out, not_90_out, 1'b0);
  or or_118 (or_118_out, not_91_out, 1'b0);
  or or_119 (or_119_out, not_92_out, 1'b0);
  or or_120 (or_120_out, not_93_out, 1'b0);
  or or_121 (or_121_out, not_94_out, 1'b0);
  or or_122 (or_122_out, not_95_out, 1'b0);
  or or_123 (or_123_out, inst[4], 1'b0);
  or or_124 (or_124_out, inst[5], 1'b0);
  or or_125 (or_125_out, not_96_out, 1'b0);
  or or_126 (or_126_out, inst[12], 1'b0);
  or or_127 (or_127_out, not_97_out, 1'b0);
  or or_128 (or_128_out, inst[14], 1'b0);
  or or_129 (or_129_out, inst[25], 1'b0);
  or or_130 (or_130_out, not_98_out, 1'b0);
  or or_131 (or_131_out, not_99_out, 1'b0);
  or or_132 (or_132_out, not_100_out, 1'b0);
  or or_133 (or_133_out, not_101_out, 1'b0);
  or or_134 (or_134_out, not_102_out, 1'b0);
  or or_135 (or_135_out, not_103_out, 1'b0);
  or or_136 (or_136_out, not_104_out, 1'b0);
  or or_137 (or_137_out, not_105_out, 1'b0);
  or or_138 (or_138_out, inst[4], 1'b0);
  or or_139 (or_139_out, inst[5], 1'b0);
  or or_140 (or_140_out, not_106_out, 1'b0);
  or or_141 (or_141_out, inst[12], 1'b0);
  or or_142 (or_142_out, not_107_out, 1'b0);
  or or_143 (or_143_out, inst[14], 1'b0);
  or or_144 (or_144_out, not_108_out, 1'b0);
  or or_145 (or_145_out, not_109_out, 1'b0);
  or or_146 (or_146_out, not_110_out, 1'b0);
  or or_147 (or_147_out, not_111_out, 1'b0);
  or or_148 (or_148_out, not_112_out, 1'b0);
  or or_149 (or_149_out, not_113_out, 1'b0);
  or or_150 (or_150_out, not_114_out, 1'b0);
  or or_151 (or_151_out, not_115_out, 1'b0);
  or or_152 (or_152_out, not_116_out, 1'b0);
  or or_153 (or_153_out, inst[4], 1'b0);
  or or_154 (or_154_out, inst[5], 1'b0);
  or or_155 (or_155_out, not_117_out, 1'b0);
  or or_156 (or_156_out, not_118_out, 1'b0);
  or or_157 (or_157_out, inst[13], 1'b0);
  or or_158 (or_158_out, inst[14], 1'b0);
  or or_159 (or_159_out, not_119_out, 1'b0);
  or or_160 (or_160_out, not_120_out, 1'b0);
  or or_161 (or_161_out, not_121_out, 1'b0);
  or or_162 (or_162_out, not_122_out, 1'b0);
  or or_163 (or_163_out, not_123_out, 1'b0);
  or or_164 (or_164_out, not_124_out, 1'b0);
  or or_165 (or_165_out, not_125_out, 1'b0);
  or or_166 (or_166_out, not_126_out, 1'b0);
  or or_167 (or_167_out, not_127_out, 1'b0);
  or or_168 (or_168_out, inst[4], 1'b0);
  or or_169 (or_169_out, inst[5], 1'b0);
  or or_170 (or_170_out, not_128_out, 1'b0);
  or or_171 (or_171_out, inst[12], 1'b0);
  or or_172 (or_172_out, inst[13], 1'b0);
  or or_173 (or_173_out, inst[14], 1'b0);
  or or_174 (or_174_out, inst[25], 1'b0);
  or or_175 (or_175_out, not_129_out, 1'b0);
  or or_176 (or_176_out, not_130_out, 1'b0);
  or or_177 (or_177_out, not_131_out, 1'b0);
  or or_178 (or_178_out, not_132_out, 1'b0);
  or or_179 (or_179_out, not_133_out, 1'b0);
  or or_180 (or_180_out, not_134_out, 1'b0);
  or or_181 (or_181_out, not_135_out, 1'b0);
  or or_182 (or_182_out, not_136_out, 1'b0);
  or or_183 (or_183_out, inst[4], 1'b0);
  or or_184 (or_184_out, inst[5], 1'b0);
  or or_185 (or_185_out, not_137_out, 1'b0);
  or or_186 (or_186_out, inst[12], 1'b0);
  or or_187 (or_187_out, inst[13], 1'b0);
  or or_188 (or_188_out, inst[14], 1'b0);
  or or_189 (or_189_out, not_138_out, 1'b0);
  or or_190 (or_190_out, not_139_out, 1'b0);
  or or_191 (or_191_out, not_140_out, 1'b0);
  or or_192 (or_192_out, not_141_out, 1'b0);
  or or_193 (or_193_out, not_142_out, 1'b0);
  or or_194 (or_194_out, not_143_out, 1'b0);
  or or_195 (or_195_out, not_144_out, 1'b0);
  or or_196 (or_196_out, not_145_out, 1'b0);
  or or_197 (or_197_out, not_146_out, 1'b0);
  or or_198 (or_198_out, not_147_out, 1'b0);
  or or_199 (or_199_out, not_148_out, 1'b0);
  or or_200 (or_200_out, not_149_out, 1'b0);
  or or_201 (or_201_out, not_150_out, 1'b0);
  or or_202 (or_202_out, not_151_out, 1'b0);
  or or_203 (or_203_out, not_152_out, 1'b0);
  or or_204 (or_204_out, inst[25], 1'b1);
  or or_205 (or_205_out, inst[26], 1'b1);
  or or_206 (or_206_out, inst[27], 1'b1);
  or or_207 (or_207_out, inst[28], 1'b1);
  or or_208 (or_208_out, inst[29], 1'b1);
  or or_209 (or_209_out, inst[30], 1'b1);
  or or_210 (or_210_out, inst[31], 1'b1);
  or or_211 (or_211_out, not_153_out, 1'b0);
  or or_212 (or_212_out, not_154_out, 1'b0);
  or or_213 (or_213_out, not_155_out, 1'b0);
  or or_214 (or_214_out, not_156_out, 1'b0);
  or or_215 (or_215_out, not_157_out, 1'b0);
  or or_216 (or_216_out, inst[12], 1'b0);
  or or_217 (or_217_out, not_158_out, 1'b0);
  or or_218 (or_218_out, not_159_out, 1'b0);
  or or_219 (or_219_out, inst[25], 1'b1);
  or or_220 (or_220_out, inst[26], 1'b1);
  or or_221 (or_221_out, inst[27], 1'b1);
  or or_222 (or_222_out, inst[28], 1'b1);
  or or_223 (or_223_out, inst[29], 1'b1);
  or or_224 (or_224_out, inst[30], 1'b1);
  or or_225 (or_225_out, inst[31], 1'b1);
  or or_226 (or_226_out, not_160_out, 1'b0);
  or or_227 (or_227_out, not_161_out, 1'b0);
  or or_228 (or_228_out, not_162_out, 1'b0);
  or or_229 (or_229_out, not_163_out, 1'b0);
  or or_230 (or_230_out, not_164_out, 1'b0);
  or or_231 (or_231_out, not_165_out, 1'b0);
  or or_232 (or_232_out, inst[13], 1'b0);
  or or_233 (or_233_out, not_166_out, 1'b0);
  or or_234 (or_234_out, inst[25], 1'b1);
  or or_235 (or_235_out, inst[26], 1'b1);
  or or_236 (or_236_out, inst[27], 1'b1);
  or or_237 (or_237_out, inst[28], 1'b1);
  or or_238 (or_238_out, inst[29], 1'b1);
  or or_239 (or_239_out, inst[30], 1'b1);
  or or_240 (or_240_out, inst[31], 1'b1);
  or or_241 (or_241_out, not_167_out, 1'b0);
  or or_242 (or_242_out, not_168_out, 1'b0);
  or or_243 (or_243_out, not_169_out, 1'b0);
  or or_244 (or_244_out, not_170_out, 1'b0);
  or or_245 (or_245_out, not_171_out, 1'b0);
  or or_246 (or_246_out, not_172_out, 1'b0);
  or or_247 (or_247_out, not_173_out, 1'b0);
  or or_248 (or_248_out, inst[14], 1'b0);
  or or_249 (or_249_out, inst[25], 1'b1);
  or or_250 (or_250_out, inst[26], 1'b1);
  or or_251 (or_251_out, inst[27], 1'b1);
  or or_252 (or_252_out, inst[28], 1'b1);
  or or_253 (or_253_out, inst[29], 1'b1);
  or or_254 (or_254_out, inst[30], 1'b1);
  or or_255 (or_255_out, inst[31], 1'b1);
  or or_256 (or_256_out, not_174_out, 1'b0);
  or or_257 (or_257_out, not_175_out, 1'b0);
  or or_258 (or_258_out, not_176_out, 1'b0);
  or or_259 (or_259_out, not_177_out, 1'b0);
  or or_260 (or_260_out, not_178_out, 1'b0);
  or or_261 (or_261_out, inst[12], 1'b0);
  or or_262 (or_262_out, not_179_out, 1'b0);
  or or_263 (or_263_out, inst[14], 1'b0);
  or or_264 (or_264_out, inst[25], 1'b1);
  or or_265 (or_265_out, inst[26], 1'b1);
  or or_266 (or_266_out, inst[27], 1'b1);
  or or_267 (or_267_out, inst[28], 1'b1);
  or or_268 (or_268_out, inst[29], 1'b1);
  or or_269 (or_269_out, inst[30], 1'b1);
  or or_270 (or_270_out, inst[31], 1'b1);
  or or_271 (or_271_out, not_180_out, 1'b0);
  or or_272 (or_272_out, not_181_out, 1'b0);
  or or_273 (or_273_out, inst[4], 1'b0);
  or or_274 (or_274_out, not_182_out, 1'b0);
  or or_275 (or_275_out, not_183_out, 1'b0);
  or or_276 (or_276_out, not_184_out, 1'b0);
  or or_277 (or_277_out, not_185_out, 1'b0);
  or or_278 (or_278_out, not_186_out, 1'b0);
  or or_279 (or_279_out, inst[25], 1'b1);
  or or_280 (or_280_out, inst[26], 1'b1);
  or or_281 (or_281_out, inst[27], 1'b1);
  or or_282 (or_282_out, inst[28], 1'b1);
  or or_283 (or_283_out, inst[29], 1'b1);
  or or_284 (or_284_out, inst[30], 1'b1);
  or or_285 (or_285_out, inst[31], 1'b1);
  or or_286 (or_286_out, not_187_out, 1'b0);
  or or_287 (or_287_out, not_188_out, 1'b0);
  or or_288 (or_288_out, inst[4], 1'b0);
  or or_289 (or_289_out, not_189_out, 1'b0);
  or or_290 (or_290_out, not_190_out, 1'b0);
  or or_291 (or_291_out, inst[12], 1'b0);
  or or_292 (or_292_out, not_191_out, 1'b0);
  or or_293 (or_293_out, not_192_out, 1'b0);
  or or_294 (or_294_out, not_193_out, 1'b0);
  or or_295 (or_295_out, not_194_out, 1'b0);
  or or_296 (or_296_out, not_195_out, 1'b0);
  or or_297 (or_297_out, not_196_out, 1'b0);
  or or_298 (or_298_out, not_197_out, 1'b0);
  or or_299 (or_299_out, not_198_out, 1'b0);
  or or_300 (or_300_out, not_199_out, 1'b0);
  or or_301 (or_301_out, not_200_out, 1'b0);
  or or_302 (or_302_out, not_201_out, 1'b0);
  or or_303 (or_303_out, inst[4], 1'b0);
  or or_304 (or_304_out, not_202_out, 1'b0);
  or or_305 (or_305_out, not_203_out, 1'b0);
  or or_306 (or_306_out, not_204_out, 1'b0);
  or or_307 (or_307_out, inst[13], 1'b0);
  or or_308 (or_308_out, not_205_out, 1'b0);
  or or_309 (or_309_out, inst[25], 1'b1);
  or or_310 (or_310_out, inst[26], 1'b1);
  or or_311 (or_311_out, inst[27], 1'b1);
  or or_312 (or_312_out, inst[28], 1'b1);
  or or_313 (or_313_out, inst[29], 1'b1);
  or or_314 (or_314_out, inst[30], 1'b1);
  or or_315 (or_315_out, inst[31], 1'b1);
  or or_316 (or_316_out, not_206_out, 1'b0);
  or or_317 (or_317_out, not_207_out, 1'b0);
  or or_318 (or_318_out, inst[4], 1'b0);
  or or_319 (or_319_out, not_208_out, 1'b0);
  or or_320 (or_320_out, not_209_out, 1'b0);
  or or_321 (or_321_out, not_210_out, 1'b0);
  or or_322 (or_322_out, not_211_out, 1'b0);
  or or_323 (or_323_out, inst[14], 1'b0);
  or or_324 (or_324_out, inst[25], 1'b1);
  or or_325 (or_325_out, inst[26], 1'b1);
  or or_326 (or_326_out, inst[27], 1'b1);
  or or_327 (or_327_out, inst[28], 1'b1);
  or or_328 (or_328_out, inst[29], 1'b1);
  or or_329 (or_329_out, inst[30], 1'b1);
  or or_330 (or_330_out, inst[31], 1'b1);
  or or_331 (or_331_out, not_212_out, 1'b0);
  or or_332 (or_332_out, not_213_out, 1'b0);
  or or_333 (or_333_out, inst[4], 1'b0);
  or or_334 (or_334_out, not_214_out, 1'b0);
  or or_335 (or_335_out, not_215_out, 1'b0);
  or or_336 (or_336_out, inst[12], 1'b0);
  or or_337 (or_337_out, not_216_out, 1'b0);
  or or_338 (or_338_out, inst[14], 1'b0);
  or or_339 (or_339_out, not_217_out, 1'b0);
  or or_340 (or_340_out, not_218_out, 1'b0);
  or or_341 (or_341_out, not_219_out, 1'b0);
  or or_342 (or_342_out, not_220_out, 1'b0);
  or or_343 (or_343_out, not_221_out, 1'b0);
  or or_344 (or_344_out, not_222_out, 1'b0);
  or or_345 (or_345_out, not_223_out, 1'b0);
  or or_346 (or_346_out, not_224_out, 1'b0);
  or or_347 (or_347_out, not_225_out, 1'b0);
  or or_348 (or_348_out, inst[4], 1'b0);
  or or_349 (or_349_out, not_226_out, 1'b0);
  or or_350 (or_350_out, not_227_out, 1'b0);
  or or_351 (or_351_out, not_228_out, 1'b0);
  or or_352 (or_352_out, inst[13], 1'b0);
  or or_353 (or_353_out, inst[14], 1'b0);
  or or_354 (or_354_out, inst[25], 1'b1);
  or or_355 (or_355_out, inst[26], 1'b1);
  or or_356 (or_356_out, inst[27], 1'b1);
  or or_357 (or_357_out, inst[28], 1'b1);
  or or_358 (or_358_out, inst[29], 1'b1);
  or or_359 (or_359_out, inst[30], 1'b1);
  or or_360 (or_360_out, inst[31], 1'b1);
  or or_361 (or_361_out, not_229_out, 1'b0);
  or or_362 (or_362_out, not_230_out, 1'b0);
  or or_363 (or_363_out, inst[4], 1'b0);
  or or_364 (or_364_out, not_231_out, 1'b0);
  or or_365 (or_365_out, not_232_out, 1'b0);
  or or_366 (or_366_out, inst[12], 1'b0);
  or or_367 (or_367_out, inst[13], 1'b0);
  or or_368 (or_368_out, inst[14], 1'b0);
  or or_369 (or_369_out, inst[25], 1'b1);
  or or_370 (or_370_out, inst[26], 1'b1);
  or or_371 (or_371_out, inst[27], 1'b1);
  or or_372 (or_372_out, inst[28], 1'b1);
  or or_373 (or_373_out, inst[29], 1'b1);
  or or_374 (or_374_out, inst[30], 1'b1);
  or or_375 (or_375_out, inst[31], 1'b1);
  or or_376 (or_376_out, not_233_out, 1'b0);
  or or_377 (or_377_out, not_234_out, 1'b0);
  or or_378 (or_378_out, not_235_out, 1'b0);
  or or_379 (or_379_out, inst[5], 1'b0);
  or or_380 (or_380_out, not_236_out, 1'b0);
  or or_381 (or_381_out, not_237_out, 1'b0);
  or or_382 (or_382_out, inst[13], 1'b0);
  or or_383 (or_383_out, not_238_out, 1'b0);
  or or_384 (or_384_out, inst[25], 1'b1);
  or or_385 (or_385_out, inst[26], 1'b1);
  or or_386 (or_386_out, inst[27], 1'b1);
  or or_387 (or_387_out, inst[28], 1'b1);
  or or_388 (or_388_out, inst[29], 1'b1);
  or or_389 (or_389_out, inst[30], 1'b1);
  or or_390 (or_390_out, inst[31], 1'b1);
  or or_391 (or_391_out, not_239_out, 1'b0);
  or or_392 (or_392_out, not_240_out, 1'b0);
  or or_393 (or_393_out, not_241_out, 1'b0);
  or or_394 (or_394_out, inst[5], 1'b0);
  or or_395 (or_395_out, inst[6], 1'b0);
  or or_396 (or_396_out, not_242_out, 1'b0);
  or or_397 (or_397_out, not_243_out, 1'b0);
  or or_398 (or_398_out, not_244_out, 1'b0);
  or or_399 (or_399_out, inst[25], 1'b1);
  or or_400 (or_400_out, inst[26], 1'b1);
  or or_401 (or_401_out, inst[27], 1'b1);
  or or_402 (or_402_out, inst[28], 1'b1);
  or or_403 (or_403_out, inst[29], 1'b1);
  or or_404 (or_404_out, inst[30], 1'b1);
  or or_405 (or_405_out, inst[31], 1'b1);
  or or_406 (or_406_out, not_245_out, 1'b0);
  or or_407 (or_407_out, not_246_out, 1'b0);
  or or_408 (or_408_out, not_247_out, 1'b0);
  or or_409 (or_409_out, inst[5], 1'b0);
  or or_410 (or_410_out, inst[6], 1'b0);
  or or_411 (or_411_out, not_248_out, 1'b0);
  or or_412 (or_412_out, not_249_out, 1'b0);
  or or_413 (or_413_out, inst[14], 1'b0);
  or or_414 (or_414_out, inst[25], 1'b1);
  or or_415 (or_415_out, inst[26], 1'b1);
  or or_416 (or_416_out, inst[27], 1'b1);
  or or_417 (or_417_out, inst[28], 1'b1);
  or or_418 (or_418_out, inst[29], 1'b1);
  or or_419 (or_419_out, inst[30], 1'b1);
  or or_420 (or_420_out, inst[31], 1'b1);
  or or_421 (or_421_out, not_250_out, 1'b0);
  or or_422 (or_422_out, not_251_out, 1'b0);
  or or_423 (or_423_out, not_252_out, 1'b0);
  or or_424 (or_424_out, inst[5], 1'b0);
  or or_425 (or_425_out, inst[6], 1'b0);
  or or_426 (or_426_out, not_253_out, 1'b0);
  or or_427 (or_427_out, inst[13], 1'b0);
  or or_428 (or_428_out, inst[14], 1'b0);
  or or_429 (or_429_out, inst[25], 1'b1);
  or or_430 (or_430_out, inst[26], 1'b1);
  or or_431 (or_431_out, inst[27], 1'b1);
  or or_432 (or_432_out, inst[28], 1'b1);
  or or_433 (or_433_out, inst[29], 1'b1);
  or or_434 (or_434_out, inst[30], 1'b1);
  or or_435 (or_435_out, inst[31], 1'b1);
  or or_436 (or_436_out, not_254_out, 1'b0);
  or or_437 (or_437_out, not_255_out, 1'b0);
  or or_438 (or_438_out, not_256_out, 1'b0);
  or or_439 (or_439_out, inst[5], 1'b0);
  or or_440 (or_440_out, inst[6], 1'b0);
  or or_441 (or_441_out, inst[12], 1'b0);
  or or_442 (or_442_out, not_257_out, 1'b0);
  or or_443 (or_443_out, not_258_out, 1'b0);
  or or_444 (or_444_out, inst[25], 1'b1);
  or or_445 (or_445_out, inst[26], 1'b1);
  or or_446 (or_446_out, inst[27], 1'b1);
  or or_447 (or_447_out, inst[28], 1'b1);
  or or_448 (or_448_out, inst[29], 1'b1);
  or or_449 (or_449_out, inst[30], 1'b1);
  or or_450 (or_450_out, inst[31], 1'b1);
  or or_451 (or_451_out, not_259_out, 1'b0);
  or or_452 (or_452_out, not_260_out, 1'b0);
  or or_453 (or_453_out, not_261_out, 1'b0);
  or or_454 (or_454_out, inst[5], 1'b0);
  or or_455 (or_455_out, inst[6], 1'b0);
  or or_456 (or_456_out, inst[12], 1'b0);
  or or_457 (or_457_out, inst[13], 1'b0);
  or or_458 (or_458_out, inst[14], 1'b0);
  or or_459 (or_459_out, inst[25], 1'b1);
  or or_460 (or_460_out, inst[26], 1'b1);
  or or_461 (or_461_out, inst[27], 1'b1);
  or or_462 (or_462_out, inst[28], 1'b1);
  or or_463 (or_463_out, inst[29], 1'b1);
  or or_464 (or_464_out, inst[30], 1'b1);
  or or_465 (or_465_out, inst[31], 1'b1);
  or or_466 (or_466_out, inst[2], 1'b0);
  or or_467 (or_467_out, not_262_out, 1'b0);
  or or_468 (or_468_out, inst[4], 1'b0);
  or or_469 (or_469_out, not_263_out, 1'b0);
  or or_470 (or_470_out, not_264_out, 1'b0);
  or or_471 (or_471_out, inst[12], 1'b1);
  or or_472 (or_472_out, inst[13], 1'b1);
  or or_473 (or_473_out, inst[14], 1'b1);
  or or_474 (or_474_out, inst[25], 1'b1);
  or or_475 (or_475_out, inst[26], 1'b1);
  or or_476 (or_476_out, inst[27], 1'b1);
  or or_477 (or_477_out, inst[28], 1'b1);
  or or_478 (or_478_out, inst[29], 1'b1);
  or or_479 (or_479_out, inst[30], 1'b1);
  or or_480 (or_480_out, inst[31], 1'b1);
  or or_481 (or_481_out, inst[2], 1'b0);
  or or_482 (or_482_out, not_265_out, 1'b0);
  or or_483 (or_483_out, inst[4], 1'b0);
  or or_484 (or_484_out, inst[5], 1'b0);
  or or_485 (or_485_out, not_266_out, 1'b0);
  or or_486 (or_486_out, inst[12], 1'b1);
  or or_487 (or_487_out, inst[13], 1'b1);
  or or_488 (or_488_out, inst[14], 1'b1);
  or or_489 (or_489_out, inst[25], 1'b1);
  or or_490 (or_490_out, inst[26], 1'b1);
  or or_491 (or_491_out, inst[27], 1'b1);
  or or_492 (or_492_out, inst[28], 1'b1);
  or or_493 (or_493_out, inst[29], 1'b1);
  or or_494 (or_494_out, inst[30], 1'b1);
  or or_495 (or_495_out, inst[31], 1'b1);
  or or_496 (or_496_out, inst[2], 1'b0);
  or or_497 (or_497_out, inst[3], 1'b0);
  or or_498 (or_498_out, not_267_out, 1'b0);
  or or_499 (or_499_out, inst[5], 1'b0);
  or or_500 (or_500_out, inst[6], 1'b0);
  or or_501 (or_501_out, inst[12], 1'b1);
  or or_502 (or_502_out, inst[13], 1'b1);
  or or_503 (or_503_out, inst[14], 1'b1);
  or or_504 (or_504_out, inst[25], 1'b1);
  or or_505 (or_505_out, inst[26], 1'b1);
  or or_506 (or_506_out, inst[27], 1'b1);
  or or_507 (or_507_out, inst[28], 1'b1);
  or or_508 (or_508_out, inst[29], 1'b1);
  or or_509 (or_509_out, inst[30], 1'b1);
  or or_510 (or_510_out, inst[31], 1'b1);
  or or_511 (or_511_out, inst[2], 1'b0);
  or or_512 (or_512_out, not_268_out, 1'b0);
  or or_513 (or_513_out, not_269_out, 1'b0);
  or or_514 (or_514_out, inst[5], 1'b0);
  or or_515 (or_515_out, inst[6], 1'b0);
  or or_516 (or_516_out, not_270_out, 1'b0);
  or or_517 (or_517_out, not_271_out, 1'b0);
  or or_518 (or_518_out, not_272_out, 1'b0);
  or or_519 (or_519_out, inst[25], 1'b1);
  or or_520 (or_520_out, inst[26], 1'b1);
  or or_521 (or_521_out, inst[27], 1'b1);
  or or_522 (or_522_out, inst[28], 1'b1);
  or or_523 (or_523_out, inst[29], 1'b1);
  or or_524 (or_524_out, inst[30], 1'b1);
  or or_525 (or_525_out, inst[31], 1'b1);
  and and_1 (add_flag, or_1_out, or_2_out, or_3_out, or_4_out, or_5_out, or_6_out, or_7_out, or_8_out, or_9_out, or_10_out, or_11_out, or_12_out, or_13_out, or_14_out, or_15_out);
  and and_2 (mul_flag, or_16_out, or_17_out, or_18_out, or_19_out, or_20_out, or_21_out, or_22_out, or_23_out, or_24_out, or_25_out, or_26_out, or_27_out, or_28_out, or_29_out, or_30_out);
  and and_3 (sub_flag, or_31_out, or_32_out, or_33_out, or_34_out, or_35_out, or_36_out, or_37_out, or_38_out, or_39_out, or_40_out, or_41_out, or_42_out, or_43_out, or_44_out, or_45_out);
  and and_4 (sll_flag, or_46_out, or_47_out, or_48_out, or_49_out, or_50_out, or_51_out, or_52_out, or_53_out, or_54_out, or_55_out, or_56_out, or_57_out, or_58_out, or_59_out, or_60_out);
  and and_5 (mulh_flag, or_61_out, or_62_out, or_63_out, or_64_out, or_65_out, or_66_out, or_67_out, or_68_out, or_69_out, or_70_out, or_71_out, or_72_out, or_73_out, or_74_out, or_75_out);
  and and_6 (mulhu_flag, or_76_out, or_77_out, or_78_out, or_79_out, or_80_out, or_81_out, or_82_out, or_83_out, or_84_out, or_85_out, or_86_out, or_87_out, or_88_out, or_89_out, or_90_out);
  and and_7 (xor_flag, or_91_out, or_92_out, or_93_out, or_94_out, or_95_out, or_96_out, or_97_out, or_98_out, or_99_out, or_100_out, or_101_out, or_102_out, or_103_out, or_104_out, or_105_out);
  and and_8 (div_flag, or_106_out, or_107_out, or_108_out, or_109_out, or_110_out, or_111_out, or_112_out, or_113_out, or_114_out, or_115_out, or_116_out, or_117_out, or_118_out, or_119_out, or_120_out);
  and and_9 (divu_flag, or_121_out, or_122_out, or_123_out, or_124_out, or_125_out, or_126_out, or_127_out, or_128_out, or_129_out, or_130_out, or_131_out, or_132_out, or_133_out, or_134_out, or_135_out);
  and and_10 (srl_flag, or_136_out, or_137_out, or_138_out, or_139_out, or_140_out, or_141_out, or_142_out, or_143_out, or_144_out, or_145_out, or_146_out, or_147_out, or_148_out, or_149_out, or_150_out);
  and and_11 (or_flag, or_151_out, or_152_out, or_153_out, or_154_out, or_155_out, or_156_out, or_157_out, or_158_out, or_159_out, or_160_out, or_161_out, or_162_out, or_163_out, or_164_out, or_165_out);
  and and_12 (remu_flag, or_166_out, or_167_out, or_168_out, or_169_out, or_170_out, or_171_out, or_172_out, or_173_out, or_174_out, or_175_out, or_176_out, or_177_out, or_178_out, or_179_out, or_180_out);
  and and_13 (and_flag, or_181_out, or_182_out, or_183_out, or_184_out, or_185_out, or_186_out, or_187_out, or_188_out, or_189_out, or_190_out, or_191_out, or_192_out, or_193_out, or_194_out, or_195_out);
  and and_14 (lb_flag, or_196_out, or_197_out, or_198_out, or_199_out, or_200_out, or_201_out, or_202_out, or_203_out, or_204_out, or_205_out, or_206_out, or_207_out, or_208_out, or_209_out, or_210_out);
  and and_15 (lh_flag, or_211_out, or_212_out, or_213_out, or_214_out, or_215_out, or_216_out, or_217_out, or_218_out, or_219_out, or_220_out, or_221_out, or_222_out, or_223_out, or_224_out, or_225_out);
  and and_16 (lw_flag, or_226_out, or_227_out, or_228_out, or_229_out, or_230_out, or_231_out, or_232_out, or_233_out, or_234_out, or_235_out, or_236_out, or_237_out, or_238_out, or_239_out, or_240_out);
  and and_17 (lbu_flag, or_241_out, or_242_out, or_243_out, or_244_out, or_245_out, or_246_out, or_247_out, or_248_out, or_249_out, or_250_out, or_251_out, or_252_out, or_253_out, or_254_out, or_255_out);
  and and_18 (lhu_flag, or_256_out, or_257_out, or_258_out, or_259_out, or_260_out, or_261_out, or_262_out, or_263_out, or_264_out, or_265_out, or_266_out, or_267_out, or_268_out, or_269_out, or_270_out);
  and and_19 (addi_flag, or_271_out, or_272_out, or_273_out, or_274_out, or_275_out, or_276_out, or_277_out, or_278_out, or_279_out, or_280_out, or_281_out, or_282_out, or_283_out, or_284_out, or_285_out);
  and and_20 (slli_flag, or_286_out, or_287_out, or_288_out, or_289_out, or_290_out, or_291_out, or_292_out, or_293_out, or_294_out, or_295_out, or_296_out, or_297_out, or_298_out, or_299_out, or_300_out);
  and and_21 (slti_flag, or_301_out, or_302_out, or_303_out, or_304_out, or_305_out, or_306_out, or_307_out, or_308_out, or_309_out, or_310_out, or_311_out, or_312_out, or_313_out, or_314_out, or_315_out);
  and and_22 (xori_flag, or_316_out, or_317_out, or_318_out, or_319_out, or_320_out, or_321_out, or_322_out, or_323_out, or_324_out, or_325_out, or_326_out, or_327_out, or_328_out, or_329_out, or_330_out);
  and and_23 (srli_flag, or_331_out, or_332_out, or_333_out, or_334_out, or_335_out, or_336_out, or_337_out, or_338_out, or_339_out, or_340_out, or_341_out, or_342_out, or_343_out, or_344_out, or_345_out);
  and and_24 (ori_flag, or_346_out, or_347_out, or_348_out, or_349_out, or_350_out, or_351_out, or_352_out, or_353_out, or_354_out, or_355_out, or_356_out, or_357_out, or_358_out, or_359_out, or_360_out);
  and and_25 (andi_flag, or_361_out, or_362_out, or_363_out, or_364_out, or_365_out, or_366_out, or_367_out, or_368_out, or_369_out, or_370_out, or_371_out, or_372_out, or_373_out, or_374_out, or_375_out);
  and and_26 (sw_flag, or_376_out, or_377_out, or_378_out, or_379_out, or_380_out, or_381_out, or_382_out, or_383_out, or_384_out, or_385_out, or_386_out, or_387_out, or_388_out, or_389_out, or_390_out);
  and and_27 (beq_flag, or_391_out, or_392_out, or_393_out, or_394_out, or_395_out, or_396_out, or_397_out, or_398_out, or_399_out, or_400_out, or_401_out, or_402_out, or_403_out, or_404_out, or_405_out);
  and and_28 (blt_flag, or_406_out, or_407_out, or_408_out, or_409_out, or_410_out, or_411_out, or_412_out, or_413_out, or_414_out, or_415_out, or_416_out, or_417_out, or_418_out, or_419_out, or_420_out);
  and and_29 (bltu_flag, or_421_out, or_422_out, or_423_out, or_424_out, or_425_out, or_426_out, or_427_out, or_428_out, or_429_out, or_430_out, or_431_out, or_432_out, or_433_out, or_434_out, or_435_out);
  and and_30 (bne_flag, or_436_out, or_437_out, or_438_out, or_439_out, or_440_out, or_441_out, or_442_out, or_443_out, or_444_out, or_445_out, or_446_out, or_447_out, or_448_out, or_449_out, or_450_out);
  and and_31 (bgeu_flag, or_451_out, or_452_out, or_453_out, or_454_out, or_455_out, or_456_out, or_457_out, or_458_out, or_459_out, or_460_out, or_461_out, or_462_out, or_463_out, or_464_out, or_465_out);
  and and_32 (auipc_flag, or_466_out, or_467_out, or_468_out, or_469_out, or_470_out, or_471_out, or_472_out, or_473_out, or_474_out, or_475_out, or_476_out, or_477_out, or_478_out, or_479_out, or_480_out);
  and and_33 (lui_flag, or_481_out, or_482_out, or_483_out, or_484_out, or_485_out, or_486_out, or_487_out, or_488_out, or_489_out, or_490_out, or_491_out, or_492_out, or_493_out, or_494_out, or_495_out);
  and and_34 (jal_flag, or_496_out, or_497_out, or_498_out, or_499_out, or_500_out, or_501_out, or_502_out, or_503_out, or_504_out, or_505_out, or_506_out, or_507_out, or_508_out, or_509_out, or_510_out);
  and and_35 (jalr_flag, or_511_out, or_512_out, or_513_out, or_514_out, or_515_out, or_516_out, or_517_out, or_518_out, or_519_out, or_520_out, or_521_out, or_522_out, or_523_out, or_524_out, or_525_out);

  // Other names for the same wires on the sheet: bit_2 = inst[2]; bit_3 = inst[3]; bit_4 = inst[4]; bit_5 = inst[5];
  //   bit_6 = inst[6]; bit_7 = inst[7]; bit_8 = inst[8]; bit_9 = inst[9]; bit_10 = inst[10]; bit_11 = inst[11];
  //   bit_12 = inst[12]; bit_13 = inst[13]; bit_14 = inst[14]; bit_15 = inst[15]; bit_16 = inst[16];
  //   bit_17 = inst[17]; bit_18 = inst[18]; bit_19 = inst[19]; bit_20 = inst[20]; bit_21 = inst[21];
  //   bit_22 = inst[22]; bit_23 = inst[23]; bit_24 = inst[24]; bit_25 = inst[25]; bit_26 = inst[26];
  //   bit_27 = inst[27]; bit_28 = inst[28]; bit_29 = inst[29]; bit_30 = inst[30]; bit_31 = inst[31]
endmodule

module ControllerOutput (
  input  add_flag,
  input  mul_flag,
  input  sub_flag,
  input  sll_flag,
  input  mulh_flag,
  input  mulhu_flag,
  input  xor_flag,
  input  div_flag,
  input  divu_flag,
  input  srl_flag,
  input  or_flag,
  input  remu_flag,
  input  and_flag,
  input  lb_flag,
  input  lh_flag,
  input  lw_flag,
  input  lbu_flag,
  input  lhu_flag,
  input  addi_flag,
  input  slli_flag,
  input  slti_flag,
  input  xori_flag,
  input  srli_flag,
  input  ori_flag,
  input  andi_flag,
  input  sw_flag,
  input  beq_flag,
  input  blt_flag,
  input  bltu_flag,
  input  bne_flag,
  input  bgeu_flag,
  input  auipc_flag,
  input  lui_flag,
  input  jal_flag,
  input  jalr_flag,
  input  breq_flag,
  input  brlt_flag,
  output PCSelOutput,
  output [2:0] ImmSelOutput,
  output BrUnOutput,
  output ASelOutput,
  output BSelOutput,
  output [3:0] ALUSelOutput,
  output MemRWOutput,
  output RegWEnOutput,
  output [1:0] WBSelOutput
);

  PCSel pcsel_1 (
    .add_flag(add_flag), .mul_flag(mul_flag), .sub_flag(sub_flag), .sll_flag(sll_flag),
    .mulh_flag(mulh_flag), .mulhu_flag(mulhu_flag), .xor_flag(xor_flag), .div_flag(div_flag),
    .divu_flag(divu_flag), .srl_flag(srl_flag), .or_flag(or_flag), .remu_flag(remu_flag),
    .and_flag(and_flag), .lb_flag(lb_flag), .lh_flag(lh_flag), .lw_flag(lw_flag), .lbu_flag(lbu_flag),
    .lhu_flag(lhu_flag), .addi_flag(addi_flag), .slli_flag(slli_flag), .slti_flag(slti_flag),
    .xori_flag(xori_flag), .srli_flag(srli_flag), .ori_flag(ori_flag), .andi_flag(andi_flag),
    .sw_flag(sw_flag), .beq_flag(beq_flag), .blt_flag(blt_flag), .bltu_flag(bltu_flag), .bne_flag(bne_flag),
    .bgeu_flag(bgeu_flag), .auipc_flag(auipc_flag), .lui_flag(lui_flag), .jal_flag(jal_flag),
    .jalr_flag(jalr_flag), .breq_flag(breq_flag), .brlt_flag(brlt_flag), .out_38(PCSelOutput));
  ImmSel immsel_1 (
    .add_flag(add_flag), .mul_flag(mul_flag), .sub_flag(sub_flag), .sll_flag(sll_flag),
    .mulh_flag(mulh_flag), .mulhu_flag(mulhu_flag), .xor_flag(xor_flag), .div_flag(div_flag),
    .divu_flag(divu_flag), .srl_flag(srl_flag), .or_flag(or_flag), .remu_flag(remu_flag),
    .and_flag(and_flag), .lb_flag(lb_flag), .lh_flag(lh_flag), .lw_flag(lw_flag), .lbu_flag(lbu_flag),
    .lhu_flag(lhu_flag), .addi_flag(addi_flag), .slli_flag(slli_flag), .slti_flag(slti_flag),
    .xori_flag(xori_flag), .srli_flag(srli_flag), .ori_flag(ori_flag), .andi_flag(andi_flag),
    .sw_flag(sw_flag), .beq_flag(beq_flag), .blt_flag(blt_flag), .bltu_flag(bltu_flag), .bne_flag(bne_flag),
    .bgeu_flag(bgeu_flag), .auipc_flag(auipc_flag), .lui_flag(lui_flag), .jal_flag(jal_flag),
    .jalr_flag(jalr_flag), .out_36(ImmSelOutput));
  BrUn brun_1 (
    .add_flag(add_flag), .mul_flag(mul_flag), .sub_flag(sub_flag), .sll_flag(sll_flag),
    .mulh_flag(mulh_flag), .mulhu_flag(mulhu_flag), .xor_flag(xor_flag), .div_flag(div_flag),
    .divu_flag(divu_flag), .srl_flag(srl_flag), .or_flag(or_flag), .remu_flag(remu_flag),
    .and_flag(and_flag), .lb_flag(lb_flag), .lh_flag(lh_flag), .lw_flag(lw_flag), .lbu_flag(lbu_flag),
    .lhu_flag(lhu_flag), .addi_flag(addi_flag), .slli_flag(slli_flag), .slti_flag(slti_flag),
    .xori_flag(xori_flag), .srli_flag(srli_flag), .ori_flag(ori_flag), .andi_flag(andi_flag),
    .sw_flag(sw_flag), .beq_flag(beq_flag), .blt_flag(blt_flag), .bltu_flag(bltu_flag), .bne_flag(bne_flag),
    .bgeu_flag(bgeu_flag), .auipc_flag(auipc_flag), .lui_flag(lui_flag), .jal_flag(jal_flag),
    .jalr_flag(jalr_flag), .out_36(BrUnOutput));
  ASel asel_1 (
    .add_flag(add_flag), .mul_flag(mul_flag), .sub_flag(sub_flag), .sll_flag(sll_flag),
    .mulh_flag(mulh_flag), .mulhu_flag(mulhu_flag), .xor_flag(xor_flag), .div_flag(div_flag),
    .divu_flag(divu_flag), .srl_flag(srl_flag), .or_flag(or_flag), .remu_flag(remu_flag),
    .and_flag(and_flag), .lb_flag(lb_flag), .lh_flag(lh_flag), .lw_flag(lw_flag), .lbu_flag(lbu_flag),
    .lhu_flag(lhu_flag), .addi_flag(addi_flag), .slli_flag(slli_flag), .slti_flag(slti_flag),
    .xori_flag(xori_flag), .srli_flag(srli_flag), .ori_flag(ori_flag), .andi_flag(andi_flag),
    .sw_flag(sw_flag), .beq_flag(beq_flag), .blt_flag(blt_flag), .bltu_flag(bltu_flag), .bne_flag(bne_flag),
    .bgeu_flag(bgeu_flag), .auipc_flag(auipc_flag), .lui_flag(lui_flag), .jal_flag(jal_flag),
    .jalr_flag(jalr_flag), .out_36(ASelOutput));
  BSel bsel_1 (
    .add_flag(add_flag), .mul_flag(mul_flag), .sub_flag(sub_flag), .sll_flag(sll_flag),
    .mulh_flag(mulh_flag), .mulhu_flag(mulhu_flag), .xor_flag(xor_flag), .div_flag(div_flag),
    .divu_flag(divu_flag), .srl_flag(srl_flag), .or_flag(or_flag), .remu_flag(remu_flag),
    .and_flag(and_flag), .lb_flag(lb_flag), .lh_flag(lh_flag), .lw_flag(lw_flag), .lbu_flag(lbu_flag),
    .lhu_flag(lhu_flag), .addi_flag(addi_flag), .slli_flag(slli_flag), .slti_flag(slti_flag),
    .xori_flag(xori_flag), .srli_flag(srli_flag), .ori_flag(ori_flag), .andi_flag(andi_flag),
    .sw_flag(sw_flag), .beq_flag(beq_flag), .blt_flag(blt_flag), .bltu_flag(bltu_flag), .bne_flag(bne_flag),
    .bgeu_flag(bgeu_flag), .auipc_flag(auipc_flag), .lui_flag(lui_flag), .jal_flag(jal_flag),
    .jalr_flag(jalr_flag), .out_36(BSelOutput));
  ALUSel alusel_1 (
    .add_flag(add_flag), .mul_flag(mul_flag), .sub_flag(sub_flag), .sll_flag(sll_flag),
    .mulh_flag(mulh_flag), .mulhu_flag(mulhu_flag), .xor_flag(xor_flag), .div_flag(div_flag),
    .divu_flag(divu_flag), .srl_flag(srl_flag), .or_flag(or_flag), .remu_flag(remu_flag),
    .and_flag(and_flag), .lb_flag(lb_flag), .lh_flag(lh_flag), .lw_flag(lw_flag), .lbu_flag(lbu_flag),
    .lhu_flag(lhu_flag), .addi_flag(addi_flag), .slli_flag(slli_flag), .slti_flag(slti_flag),
    .xori_flag(xori_flag), .srli_flag(srli_flag), .ori_flag(ori_flag), .andi_flag(andi_flag),
    .sw_flag(sw_flag), .beq_flag(beq_flag), .blt_flag(blt_flag), .bltu_flag(bltu_flag), .bne_flag(bne_flag),
    .bgeu_flag(bgeu_flag), .auipc_flag(auipc_flag), .lui_flag(lui_flag), .jal_flag(jal_flag),
    .jalr_flag(jalr_flag), .out_36(ALUSelOutput));
  MemRW memrw_1 (
    .add_flag(add_flag), .mul_flag(mul_flag), .sub_flag(sub_flag), .sll_flag(sll_flag),
    .mulh_flag(mulh_flag), .mulhu_flag(mulhu_flag), .xor_flag(xor_flag), .div_flag(div_flag),
    .divu_flag(divu_flag), .srl_flag(srl_flag), .or_flag(or_flag), .remu_flag(remu_flag),
    .and_flag(and_flag), .lb_flag(lb_flag), .lh_flag(lh_flag), .lw_flag(lw_flag), .lbu_flag(lbu_flag),
    .lhu_flag(lhu_flag), .addi_flag(addi_flag), .slli_flag(slli_flag), .slti_flag(slti_flag),
    .xori_flag(xori_flag), .srli_flag(srli_flag), .ori_flag(ori_flag), .andi_flag(andi_flag),
    .sw_flag(sw_flag), .beq_flag(beq_flag), .blt_flag(blt_flag), .bltu_flag(bltu_flag), .bne_flag(bne_flag),
    .bgeu_flag(bgeu_flag), .auipc_flag(auipc_flag), .lui_flag(lui_flag), .jal_flag(jal_flag),
    .jalr_flag(jalr_flag), .out_36(MemRWOutput));
  RegWEn regwen_1 (
    .add_flag(add_flag), .mul_flag(mul_flag), .sub_flag(sub_flag), .sll_flag(sll_flag),
    .mulh_flag(mulh_flag), .mulhu_flag(mulhu_flag), .xor_flag(xor_flag), .div_flag(div_flag),
    .divu_flag(divu_flag), .srl_flag(srl_flag), .or_flag(or_flag), .remu_flag(remu_flag),
    .and_flag(and_flag), .lb_flag(lb_flag), .lh_flag(lh_flag), .lw_flag(lw_flag), .lbu_flag(lbu_flag),
    .lhu_flag(lhu_flag), .addi_flag(addi_flag), .slli_flag(slli_flag), .slti_flag(slti_flag),
    .xori_flag(xori_flag), .srli_flag(srli_flag), .ori_flag(ori_flag), .andi_flag(andi_flag),
    .sw_flag(sw_flag), .beq_flag(beq_flag), .blt_flag(blt_flag), .bltu_flag(bltu_flag), .bne_flag(bne_flag),
    .bgeu_flag(bgeu_flag), .auipc_flag(auipc_flag), .lui_flag(lui_flag), .jal_flag(jal_flag),
    .jalr_flag(jalr_flag), .out_36(RegWEnOutput));
  WBSel wbsel_1 (
    .add_flag(add_flag), .mul_flag(mul_flag), .sub_flag(sub_flag), .sll_flag(sll_flag),
    .mulh_flag(mulh_flag), .mulhu_flag(mulhu_flag), .xor_flag(xor_flag), .div_flag(div_flag),
    .divu_flag(divu_flag), .srl_flag(srl_flag), .or_flag(or_flag), .remu_flag(remu_flag),
    .and_flag(and_flag), .lb_flag(lb_flag), .lh_flag(lh_flag), .lw_flag(lw_flag), .lbu_flag(lbu_flag),
    .lhu_flag(lhu_flag), .addi_flag(addi_flag), .slli_flag(slli_flag), .slti_flag(slti_flag),
    .xori_flag(xori_flag), .srli_flag(srli_flag), .ori_flag(ori_flag), .andi_flag(andi_flag),
    .sw_flag(sw_flag), .beq_flag(beq_flag), .blt_flag(blt_flag), .bltu_flag(bltu_flag), .bne_flag(bne_flag),
    .bgeu_flag(bgeu_flag), .auipc_flag(auipc_flag), .lui_flag(lui_flag), .jal_flag(jal_flag),
    .jalr_flag(jalr_flag), .out_36(WBSelOutput));

  // Other names for the same wires on the sheet: BrEq = breq_flag; BrLT = brlt_flag
endmodule

module PCSel (
  input  add_flag,
  input  mul_flag,
  input  sub_flag,
  input  sll_flag,
  input  mulh_flag,
  input  mulhu_flag,
  input  xor_flag,
  input  div_flag,
  input  divu_flag,
  input  srl_flag,
  input  or_flag,
  input  remu_flag,
  input  and_flag,
  input  lb_flag,
  input  lh_flag,
  input  lw_flag,
  input  lbu_flag,
  input  lhu_flag,
  input  addi_flag,
  input  slli_flag,
  input  slti_flag,
  input  xori_flag,
  input  srli_flag,
  input  ori_flag,
  input  andi_flag,
  input  sw_flag,
  input  beq_flag,
  input  blt_flag,
  input  bltu_flag,
  input  bne_flag,
  input  bgeu_flag,
  input  auipc_flag,
  input  lui_flag,
  input  jal_flag,
  input  jalr_flag,
  input  breq_flag,
  input  brlt_flag,
  output out_38
);

  wire and_1_out, and_2_out, and_3_out, and_4_out, and_5_out, and_6_out, and_7_out, and_8_out, and_9_out,
       and_10_out, and_11_out, and_12_out, and_13_out, and_14_out, and_15_out, and_16_out, and_17_out,
       and_18_out, and_19_out, and_20_out, and_21_out, and_22_out, and_23_out, and_24_out, and_25_out,
       and_26_out, and_27_out, and_28_out, and_29_out, and_30_out, and_31_out, and_32_out, and_33_out,
       and_34_out, and_35_out, BrGE, BrNe, expand_1_1_out_2, expand_1_2_out_2, expand_1_3_out_2,
       expand_1_4_out_2, expand_1_5_out_2, expand_1_6_out_2, expand_1_7_out_2, expand_1_8_out_2,
       expand_1_9_out_2, expand_1_10_out_2, expand_1_11_out_2, expand_1_12_out_2, expand_1_13_out_2,
       expand_1_14_out_2, expand_1_15_out_2, expand_1_16_out_2, expand_1_17_out_2, expand_1_18_out_2,
       expand_1_19_out_2, expand_1_20_out_2, expand_1_21_out_2, expand_1_22_out_2, expand_1_23_out_2,
       expand_1_24_out_2, expand_1_25_out_2, expand_1_26_out_2, expand_1_27_out_2, expand_1_28_out_2,
       expand_1_29_out_2, expand_1_30_out_2, expand_1_31_out_2, expand_1_32_out_2, expand_1_33_out_2,
       expand_1_34_out_2, expand_1_35_out_2, or_1_out;

  not not_1 (BrNe, breq_flag);
  not not_2 (BrGE, brlt_flag);
  expand_1 expand_1_1 (.in_1(add_flag), .out_2(expand_1_1_out_2));
  expand_1 expand_1_2 (.in_1(mul_flag), .out_2(expand_1_2_out_2));
  expand_1 expand_1_3 (.in_1(sub_flag), .out_2(expand_1_3_out_2));
  expand_1 expand_1_4 (.in_1(sll_flag), .out_2(expand_1_4_out_2));
  expand_1 expand_1_5 (.in_1(mulh_flag), .out_2(expand_1_5_out_2));
  expand_1 expand_1_6 (.in_1(mulhu_flag), .out_2(expand_1_6_out_2));
  expand_1 expand_1_7 (.in_1(xor_flag), .out_2(expand_1_7_out_2));
  expand_1 expand_1_8 (.in_1(div_flag), .out_2(expand_1_8_out_2));
  expand_1 expand_1_9 (.in_1(divu_flag), .out_2(expand_1_9_out_2));
  expand_1 expand_1_10 (.in_1(srl_flag), .out_2(expand_1_10_out_2));
  expand_1 expand_1_11 (.in_1(or_flag), .out_2(expand_1_11_out_2));
  expand_1 expand_1_12 (.in_1(remu_flag), .out_2(expand_1_12_out_2));
  expand_1 expand_1_13 (.in_1(and_flag), .out_2(expand_1_13_out_2));
  expand_1 expand_1_14 (.in_1(lb_flag), .out_2(expand_1_14_out_2));
  expand_1 expand_1_15 (.in_1(lh_flag), .out_2(expand_1_15_out_2));
  expand_1 expand_1_16 (.in_1(lw_flag), .out_2(expand_1_16_out_2));
  expand_1 expand_1_17 (.in_1(lbu_flag), .out_2(expand_1_17_out_2));
  expand_1 expand_1_18 (.in_1(lhu_flag), .out_2(expand_1_18_out_2));
  expand_1 expand_1_19 (.in_1(addi_flag), .out_2(expand_1_19_out_2));
  expand_1 expand_1_20 (.in_1(slli_flag), .out_2(expand_1_20_out_2));
  expand_1 expand_1_21 (.in_1(slti_flag), .out_2(expand_1_21_out_2));
  expand_1 expand_1_22 (.in_1(xori_flag), .out_2(expand_1_22_out_2));
  expand_1 expand_1_23 (.in_1(srli_flag), .out_2(expand_1_23_out_2));
  expand_1 expand_1_24 (.in_1(ori_flag), .out_2(expand_1_24_out_2));
  expand_1 expand_1_25 (.in_1(andi_flag), .out_2(expand_1_25_out_2));
  expand_1 expand_1_26 (.in_1(sw_flag), .out_2(expand_1_26_out_2));
  expand_1 expand_1_27 (.in_1(beq_flag), .out_2(expand_1_27_out_2));
  expand_1 expand_1_28 (.in_1(blt_flag), .out_2(expand_1_28_out_2));
  expand_1 expand_1_29 (.in_1(bltu_flag), .out_2(expand_1_29_out_2));
  expand_1 expand_1_30 (.in_1(bne_flag), .out_2(expand_1_30_out_2));
  expand_1 expand_1_31 (.in_1(bgeu_flag), .out_2(expand_1_31_out_2));
  expand_1 expand_1_32 (.in_1(auipc_flag), .out_2(expand_1_32_out_2));
  expand_1 expand_1_33 (.in_1(lui_flag), .out_2(expand_1_33_out_2));
  expand_1 expand_1_34 (.in_1(jal_flag), .out_2(expand_1_34_out_2));
  expand_1 expand_1_35 (.in_1(jalr_flag), .out_2(expand_1_35_out_2));
  and and_1 (and_1_out, expand_1_1_out_2, 1'b0);
  and and_2 (and_2_out, expand_1_2_out_2, 1'b0);
  and and_3 (and_3_out, expand_1_3_out_2, 1'b0);
  and and_4 (and_4_out, expand_1_4_out_2, 1'b0);
  and and_5 (and_5_out, expand_1_5_out_2, 1'b0);
  and and_6 (and_6_out, expand_1_6_out_2, 1'b0);
  and and_7 (and_7_out, expand_1_7_out_2, 1'b0);
  and and_8 (and_8_out, expand_1_8_out_2, 1'b0);
  and and_9 (and_9_out, expand_1_9_out_2, 1'b0);
  and and_10 (and_10_out, expand_1_10_out_2, 1'b0);
  and and_11 (and_11_out, expand_1_11_out_2, 1'b0);
  and and_12 (and_12_out, expand_1_12_out_2, 1'b0);
  and and_13 (and_13_out, expand_1_13_out_2, 1'b0);
  and and_14 (and_14_out, expand_1_14_out_2, 1'b0);
  and and_15 (and_15_out, expand_1_15_out_2, 1'b0);
  and and_16 (and_16_out, expand_1_16_out_2, 1'b0);
  and and_17 (and_17_out, expand_1_17_out_2, 1'b0);
  and and_18 (and_18_out, expand_1_18_out_2, 1'b0);
  and and_19 (and_19_out, expand_1_19_out_2, 1'b0);
  and and_20 (and_20_out, expand_1_20_out_2, 1'b0);
  and and_21 (and_21_out, expand_1_21_out_2, 1'b0);
  and and_22 (and_22_out, expand_1_22_out_2, 1'b0);
  and and_23 (and_23_out, expand_1_23_out_2, 1'b0);
  and and_24 (and_24_out, expand_1_24_out_2, 1'b0);
  and and_25 (and_25_out, expand_1_25_out_2, 1'b0);
  and and_26 (and_26_out, expand_1_26_out_2, 1'b0);
  and and_27 (and_27_out, expand_1_27_out_2, breq_flag, 1'b1);
  and and_28 (and_28_out, expand_1_28_out_2, brlt_flag, 1'b1);
  and and_29 (and_29_out, expand_1_29_out_2, brlt_flag, 1'b1);
  and and_30 (and_30_out, expand_1_30_out_2, BrNe, 1'b1);
  and and_31 (and_31_out, expand_1_31_out_2, BrGE, 1'b1);
  and and_32 (and_32_out, expand_1_32_out_2, 1'b0);
  and and_33 (and_33_out, expand_1_33_out_2, 1'b0);
  and and_34 (and_34_out, expand_1_34_out_2, 1'b1);
  and and_35 (and_35_out, expand_1_35_out_2, 1'b1);
  or or_1 (or_1_out, and_32_out, and_33_out, and_34_out, and_35_out);
  or or_2 (out_38, and_1_out, and_2_out, and_3_out, and_4_out, and_5_out, and_6_out, and_7_out, and_8_out, and_9_out, and_10_out, and_11_out, and_12_out, and_13_out, and_14_out, and_15_out, and_16_out, and_17_out, and_18_out, and_19_out, and_20_out, and_21_out, and_22_out, and_23_out, and_24_out, and_25_out, and_26_out, and_27_out, and_28_out, and_29_out, and_30_out, and_31_out, or_1_out);

  // Other names for the same wires on the sheet: BrEq = breq_flag; BrLT = brlt_flag

  // Notes on the sheet:
  //   Zero presents PC + 4, One presents result of ALU.
endmodule

module ImmSel (
  input  add_flag,
  input  mul_flag,
  input  sub_flag,
  input  sll_flag,
  input  mulh_flag,
  input  mulhu_flag,
  input  xor_flag,
  input  div_flag,
  input  divu_flag,
  input  srl_flag,
  input  or_flag,
  input  remu_flag,
  input  and_flag,
  input  lb_flag,
  input  lh_flag,
  input  lw_flag,
  input  lbu_flag,
  input  lhu_flag,
  input  addi_flag,
  input  slli_flag,
  input  slti_flag,
  input  xori_flag,
  input  srli_flag,
  input  ori_flag,
  input  andi_flag,
  input  sw_flag,
  input  beq_flag,
  input  blt_flag,
  input  bltu_flag,
  input  bne_flag,
  input  bgeu_flag,
  input  auipc_flag,
  input  lui_flag,
  input  jal_flag,
  input  jalr_flag,
  output [2:0] out_36
);

  wire [2:0] and_1_out, and_2_out, and_3_out, and_4_out, and_5_out, and_6_out, and_7_out, and_8_out,
       and_9_out, and_10_out, and_11_out, and_12_out, and_13_out, and_14_out, and_15_out, and_16_out,
       and_17_out, and_18_out, and_19_out, and_20_out, and_21_out, and_22_out, and_23_out, and_24_out,
       and_25_out, and_26_out, and_27_out, and_28_out, and_29_out, and_30_out, and_31_out, and_32_out,
       and_33_out, and_34_out, and_35_out, expand_3_1_out_2, expand_3_2_out_2, expand_3_3_out_2,
       expand_3_4_out_2, expand_3_5_out_2, expand_3_6_out_2, expand_3_7_out_2, expand_3_8_out_2,
       expand_3_9_out_2, expand_3_10_out_2, expand_3_11_out_2, expand_3_12_out_2, expand_3_13_out_2,
       expand_3_14_out_2, expand_3_15_out_2, expand_3_16_out_2, expand_3_17_out_2, expand_3_18_out_2,
       expand_3_19_out_2, expand_3_20_out_2, expand_3_21_out_2, expand_3_22_out_2, expand_3_23_out_2,
       expand_3_24_out_2, expand_3_25_out_2, expand_3_26_out_2, expand_3_27_out_2, expand_3_28_out_2,
       expand_3_29_out_2, expand_3_30_out_2, expand_3_31_out_2, expand_3_32_out_2, expand_3_33_out_2,
       expand_3_34_out_2, expand_3_35_out_2, or_1_out;

  expand_3 expand_3_1 (.in_1(add_flag), .out_2(expand_3_1_out_2));
  expand_3 expand_3_2 (.in_1(mul_flag), .out_2(expand_3_2_out_2));
  expand_3 expand_3_3 (.in_1(sub_flag), .out_2(expand_3_3_out_2));
  expand_3 expand_3_4 (.in_1(sll_flag), .out_2(expand_3_4_out_2));
  expand_3 expand_3_5 (.in_1(mulh_flag), .out_2(expand_3_5_out_2));
  expand_3 expand_3_6 (.in_1(mulhu_flag), .out_2(expand_3_6_out_2));
  expand_3 expand_3_7 (.in_1(xor_flag), .out_2(expand_3_7_out_2));
  expand_3 expand_3_8 (.in_1(div_flag), .out_2(expand_3_8_out_2));
  expand_3 expand_3_9 (.in_1(divu_flag), .out_2(expand_3_9_out_2));
  expand_3 expand_3_10 (.in_1(srl_flag), .out_2(expand_3_10_out_2));
  expand_3 expand_3_11 (.in_1(or_flag), .out_2(expand_3_11_out_2));
  expand_3 expand_3_12 (.in_1(remu_flag), .out_2(expand_3_12_out_2));
  expand_3 expand_3_13 (.in_1(and_flag), .out_2(expand_3_13_out_2));
  expand_3 expand_3_14 (.in_1(lb_flag), .out_2(expand_3_14_out_2));
  expand_3 expand_3_15 (.in_1(lh_flag), .out_2(expand_3_15_out_2));
  expand_3 expand_3_16 (.in_1(lw_flag), .out_2(expand_3_16_out_2));
  expand_3 expand_3_17 (.in_1(lbu_flag), .out_2(expand_3_17_out_2));
  expand_3 expand_3_18 (.in_1(lhu_flag), .out_2(expand_3_18_out_2));
  expand_3 expand_3_19 (.in_1(addi_flag), .out_2(expand_3_19_out_2));
  expand_3 expand_3_20 (.in_1(slli_flag), .out_2(expand_3_20_out_2));
  expand_3 expand_3_21 (.in_1(slti_flag), .out_2(expand_3_21_out_2));
  expand_3 expand_3_22 (.in_1(xori_flag), .out_2(expand_3_22_out_2));
  expand_3 expand_3_23 (.in_1(srli_flag), .out_2(expand_3_23_out_2));
  expand_3 expand_3_24 (.in_1(ori_flag), .out_2(expand_3_24_out_2));
  expand_3 expand_3_25 (.in_1(andi_flag), .out_2(expand_3_25_out_2));
  expand_3 expand_3_26 (.in_1(sw_flag), .out_2(expand_3_26_out_2));
  expand_3 expand_3_27 (.in_1(beq_flag), .out_2(expand_3_27_out_2));
  expand_3 expand_3_28 (.in_1(blt_flag), .out_2(expand_3_28_out_2));
  expand_3 expand_3_29 (.in_1(bltu_flag), .out_2(expand_3_29_out_2));
  expand_3 expand_3_30 (.in_1(bne_flag), .out_2(expand_3_30_out_2));
  expand_3 expand_3_31 (.in_1(bgeu_flag), .out_2(expand_3_31_out_2));
  expand_3 expand_3_32 (.in_1(auipc_flag), .out_2(expand_3_32_out_2));
  expand_3 expand_3_33 (.in_1(lui_flag), .out_2(expand_3_33_out_2));
  expand_3 expand_3_34 (.in_1(jal_flag), .out_2(expand_3_34_out_2));
  expand_3 expand_3_35 (.in_1(jalr_flag), .out_2(expand_3_35_out_2));
  assign and_1_out = expand_3_1_out_2 & 3'b000;  // AND_Gate and_1, 3 bits wide
  assign and_2_out = expand_3_2_out_2 & 3'b000;  // AND_Gate and_2, 3 bits wide
  assign and_3_out = expand_3_3_out_2 & 3'b000;  // AND_Gate and_3, 3 bits wide
  assign and_4_out = expand_3_4_out_2 & 3'b000;  // AND_Gate and_4, 3 bits wide
  assign and_5_out = expand_3_5_out_2 & 3'b000;  // AND_Gate and_5, 3 bits wide
  assign and_6_out = expand_3_6_out_2 & 3'b000;  // AND_Gate and_6, 3 bits wide
  assign and_7_out = expand_3_7_out_2 & 3'b000;  // AND_Gate and_7, 3 bits wide
  assign and_8_out = expand_3_8_out_2 & 3'b000;  // AND_Gate and_8, 3 bits wide
  assign and_9_out = expand_3_9_out_2 & 3'b000;  // AND_Gate and_9, 3 bits wide
  assign and_10_out = expand_3_10_out_2 & 3'b000;  // AND_Gate and_10, 3 bits wide
  assign and_11_out = expand_3_11_out_2 & 3'b000;  // AND_Gate and_11, 3 bits wide
  assign and_12_out = expand_3_12_out_2 & 3'b000;  // AND_Gate and_12, 3 bits wide
  assign and_13_out = expand_3_13_out_2 & 3'b000;  // AND_Gate and_13, 3 bits wide
  assign and_14_out = expand_3_14_out_2 & 3'b000;  // AND_Gate and_14, 3 bits wide
  assign and_15_out = expand_3_15_out_2 & 3'b000;  // AND_Gate and_15, 3 bits wide
  assign and_16_out = expand_3_16_out_2 & 3'b000;  // AND_Gate and_16, 3 bits wide
  assign and_17_out = expand_3_17_out_2 & 3'b000;  // AND_Gate and_17, 3 bits wide
  assign and_18_out = expand_3_18_out_2 & 3'b000;  // AND_Gate and_18, 3 bits wide
  assign and_19_out = expand_3_19_out_2 & 3'b000;  // AND_Gate and_19, 3 bits wide
  assign and_20_out = expand_3_20_out_2 & 3'b000;  // AND_Gate and_20, 3 bits wide
  assign and_21_out = expand_3_21_out_2 & 3'b000;  // AND_Gate and_21, 3 bits wide
  assign and_22_out = expand_3_22_out_2 & 3'b000;  // AND_Gate and_22, 3 bits wide
  assign and_23_out = expand_3_23_out_2 & 3'b000;  // AND_Gate and_23, 3 bits wide
  assign and_24_out = expand_3_24_out_2 & 3'b000;  // AND_Gate and_24, 3 bits wide
  assign and_25_out = expand_3_25_out_2 & 3'b000;  // AND_Gate and_25, 3 bits wide
  assign and_26_out = expand_3_26_out_2 & 3'b001;  // AND_Gate and_26, 3 bits wide
  assign and_27_out = expand_3_27_out_2 & 3'b010;  // AND_Gate and_27, 3 bits wide
  assign and_28_out = expand_3_28_out_2 & 3'b010;  // AND_Gate and_28, 3 bits wide
  assign and_29_out = expand_3_29_out_2 & 3'b010;  // AND_Gate and_29, 3 bits wide
  assign and_30_out = expand_3_30_out_2 & 3'b010;  // AND_Gate and_30, 3 bits wide
  assign and_31_out = expand_3_31_out_2 & 3'b010;  // AND_Gate and_31, 3 bits wide
  assign and_32_out = expand_3_32_out_2 & 3'b100;  // AND_Gate and_32, 3 bits wide
  assign and_33_out = expand_3_33_out_2 & 3'b100;  // AND_Gate and_33, 3 bits wide
  assign and_34_out = expand_3_34_out_2 & 3'b011;  // AND_Gate and_34, 3 bits wide
  assign and_35_out = expand_3_35_out_2 & 3'b000;  // AND_Gate and_35, 3 bits wide
  assign or_1_out = and_32_out | and_33_out | and_34_out | and_35_out;  // OR_Gate or_1, 3 bits wide
  assign out_36 = and_1_out | and_2_out | and_3_out | and_4_out | and_5_out | and_6_out | and_7_out | and_8_out | and_9_out | and_10_out | and_11_out | and_12_out | and_13_out | and_14_out | and_15_out | and_16_out | and_17_out | and_18_out | and_19_out | and_20_out | and_21_out | and_22_out | and_23_out | and_24_out | and_25_out | and_26_out | and_27_out | and_28_out | and_29_out | and_30_out | and_31_out | or_1_out;  // OR_Gate or_2, 3 bits wide

  // Notes on the sheet:
  //   Zero presents Unsigned and Type I, One presents Type S, Two presents Type B, Three presents Type J, Four presents Type U.
endmodule

module BrUn (
  input  add_flag,
  input  mul_flag,
  input  sub_flag,
  input  sll_flag,
  input  mulh_flag,
  input  mulhu_flag,
  input  xor_flag,
  input  div_flag,
  input  divu_flag,
  input  srl_flag,
  input  or_flag,
  input  remu_flag,
  input  and_flag,
  input  lb_flag,
  input  lh_flag,
  input  lw_flag,
  input  lbu_flag,
  input  lhu_flag,
  input  addi_flag,
  input  slli_flag,
  input  slti_flag,
  input  xori_flag,
  input  srli_flag,
  input  ori_flag,
  input  andi_flag,
  input  sw_flag,
  input  beq_flag,
  input  blt_flag,
  input  bltu_flag,
  input  bne_flag,
  input  bgeu_flag,
  input  auipc_flag,
  input  lui_flag,
  input  jal_flag,
  input  jalr_flag,
  output out_36
);

  wire and_1_out, and_2_out, and_3_out, and_4_out, and_5_out, and_6_out, and_7_out, and_8_out, and_9_out,
       and_10_out, and_11_out, and_12_out, and_13_out, and_14_out, and_15_out, and_16_out, and_17_out,
       and_18_out, and_19_out, and_20_out, and_21_out, and_22_out, and_23_out, and_24_out, and_25_out,
       and_26_out, and_27_out, and_28_out, and_29_out, and_30_out, and_31_out, and_32_out, and_33_out,
       and_34_out, and_35_out, expand_1_1_out_2, expand_1_2_out_2, expand_1_3_out_2, expand_1_4_out_2,
       expand_1_5_out_2, expand_1_6_out_2, expand_1_7_out_2, expand_1_8_out_2, expand_1_9_out_2,
       expand_1_10_out_2, expand_1_11_out_2, expand_1_12_out_2, expand_1_13_out_2, expand_1_14_out_2,
       expand_1_15_out_2, expand_1_16_out_2, expand_1_17_out_2, expand_1_18_out_2, expand_1_19_out_2,
       expand_1_20_out_2, expand_1_21_out_2, expand_1_22_out_2, expand_1_23_out_2, expand_1_24_out_2,
       expand_1_25_out_2, expand_1_26_out_2, expand_1_27_out_2, expand_1_28_out_2, expand_1_29_out_2,
       expand_1_30_out_2, expand_1_31_out_2, expand_1_32_out_2, expand_1_33_out_2, expand_1_34_out_2,
       expand_1_35_out_2, or_1_out;

  expand_1 expand_1_1 (.in_1(add_flag), .out_2(expand_1_1_out_2));
  expand_1 expand_1_2 (.in_1(mul_flag), .out_2(expand_1_2_out_2));
  expand_1 expand_1_3 (.in_1(sub_flag), .out_2(expand_1_3_out_2));
  expand_1 expand_1_4 (.in_1(sll_flag), .out_2(expand_1_4_out_2));
  expand_1 expand_1_5 (.in_1(mulh_flag), .out_2(expand_1_5_out_2));
  expand_1 expand_1_6 (.in_1(mulhu_flag), .out_2(expand_1_6_out_2));
  expand_1 expand_1_7 (.in_1(xor_flag), .out_2(expand_1_7_out_2));
  expand_1 expand_1_8 (.in_1(div_flag), .out_2(expand_1_8_out_2));
  expand_1 expand_1_9 (.in_1(divu_flag), .out_2(expand_1_9_out_2));
  expand_1 expand_1_10 (.in_1(srl_flag), .out_2(expand_1_10_out_2));
  expand_1 expand_1_11 (.in_1(or_flag), .out_2(expand_1_11_out_2));
  expand_1 expand_1_12 (.in_1(remu_flag), .out_2(expand_1_12_out_2));
  expand_1 expand_1_13 (.in_1(and_flag), .out_2(expand_1_13_out_2));
  expand_1 expand_1_14 (.in_1(lb_flag), .out_2(expand_1_14_out_2));
  expand_1 expand_1_15 (.in_1(lh_flag), .out_2(expand_1_15_out_2));
  expand_1 expand_1_16 (.in_1(lw_flag), .out_2(expand_1_16_out_2));
  expand_1 expand_1_17 (.in_1(lbu_flag), .out_2(expand_1_17_out_2));
  expand_1 expand_1_18 (.in_1(lhu_flag), .out_2(expand_1_18_out_2));
  expand_1 expand_1_19 (.in_1(addi_flag), .out_2(expand_1_19_out_2));
  expand_1 expand_1_20 (.in_1(slli_flag), .out_2(expand_1_20_out_2));
  expand_1 expand_1_21 (.in_1(slti_flag), .out_2(expand_1_21_out_2));
  expand_1 expand_1_22 (.in_1(xori_flag), .out_2(expand_1_22_out_2));
  expand_1 expand_1_23 (.in_1(srli_flag), .out_2(expand_1_23_out_2));
  expand_1 expand_1_24 (.in_1(ori_flag), .out_2(expand_1_24_out_2));
  expand_1 expand_1_25 (.in_1(andi_flag), .out_2(expand_1_25_out_2));
  expand_1 expand_1_26 (.in_1(sw_flag), .out_2(expand_1_26_out_2));
  expand_1 expand_1_27 (.in_1(beq_flag), .out_2(expand_1_27_out_2));
  expand_1 expand_1_28 (.in_1(blt_flag), .out_2(expand_1_28_out_2));
  expand_1 expand_1_29 (.in_1(bltu_flag), .out_2(expand_1_29_out_2));
  expand_1 expand_1_30 (.in_1(bne_flag), .out_2(expand_1_30_out_2));
  expand_1 expand_1_31 (.in_1(bgeu_flag), .out_2(expand_1_31_out_2));
  expand_1 expand_1_32 (.in_1(auipc_flag), .out_2(expand_1_32_out_2));
  expand_1 expand_1_33 (.in_1(lui_flag), .out_2(expand_1_33_out_2));
  expand_1 expand_1_34 (.in_1(jal_flag), .out_2(expand_1_34_out_2));
  expand_1 expand_1_35 (.in_1(jalr_flag), .out_2(expand_1_35_out_2));
  and and_1 (and_1_out, expand_1_1_out_2, 1'b0);
  and and_2 (and_2_out, expand_1_2_out_2, 1'b0);
  and and_3 (and_3_out, expand_1_3_out_2, 1'b0);
  and and_4 (and_4_out, expand_1_4_out_2, 1'b0);
  and and_5 (and_5_out, expand_1_5_out_2, 1'b0);
  and and_6 (and_6_out, expand_1_6_out_2, 1'b0);
  and and_7 (and_7_out, expand_1_7_out_2, 1'b0);
  and and_8 (and_8_out, expand_1_8_out_2, 1'b0);
  and and_9 (and_9_out, expand_1_9_out_2, 1'b0);
  and and_10 (and_10_out, expand_1_10_out_2, 1'b0);
  and and_11 (and_11_out, expand_1_11_out_2, 1'b0);
  and and_12 (and_12_out, expand_1_12_out_2, 1'b0);
  and and_13 (and_13_out, expand_1_13_out_2, 1'b0);
  and and_14 (and_14_out, expand_1_14_out_2, 1'b0);
  and and_15 (and_15_out, expand_1_15_out_2, 1'b0);
  and and_16 (and_16_out, expand_1_16_out_2, 1'b0);
  and and_17 (and_17_out, expand_1_17_out_2, 1'b0);
  and and_18 (and_18_out, expand_1_18_out_2, 1'b0);
  and and_19 (and_19_out, expand_1_19_out_2, 1'b0);
  and and_20 (and_20_out, expand_1_20_out_2, 1'b0);
  and and_21 (and_21_out, expand_1_21_out_2, 1'b0);
  and and_22 (and_22_out, expand_1_22_out_2, 1'b0);
  and and_23 (and_23_out, expand_1_23_out_2, 1'b0);
  and and_24 (and_24_out, expand_1_24_out_2, 1'b0);
  and and_25 (and_25_out, expand_1_25_out_2, 1'b0);
  and and_26 (and_26_out, expand_1_26_out_2, 1'b0);
  and and_27 (and_27_out, expand_1_27_out_2, 1'b1);
  and and_28 (and_28_out, expand_1_28_out_2, 1'b1);
  and and_29 (and_29_out, expand_1_29_out_2, 1'b0);
  and and_30 (and_30_out, expand_1_30_out_2, 1'b1);
  and and_31 (and_31_out, expand_1_31_out_2, 1'b0);
  and and_32 (and_32_out, expand_1_32_out_2, 1'b0);
  and and_33 (and_33_out, expand_1_33_out_2, 1'b0);
  and and_34 (and_34_out, expand_1_34_out_2, 1'b0);
  and and_35 (and_35_out, expand_1_35_out_2, 1'b0);
  or or_1 (or_1_out, and_32_out, and_33_out, and_34_out, and_35_out);
  or or_2 (out_36, and_1_out, and_2_out, and_3_out, and_4_out, and_5_out, and_6_out, and_7_out, and_8_out, and_9_out, and_10_out, and_11_out, and_12_out, and_13_out, and_14_out, and_15_out, and_16_out, and_17_out, and_18_out, and_19_out, and_20_out, and_21_out, and_22_out, and_23_out, and_24_out, and_25_out, and_26_out, and_27_out, and_28_out, and_29_out, and_30_out, and_31_out, or_1_out);

  // Notes on the sheet:
  //   Zero presents Unsigned and Undefine, One presents Signed.
endmodule

module ASel (
  input  add_flag,
  input  mul_flag,
  input  sub_flag,
  input  sll_flag,
  input  mulh_flag,
  input  mulhu_flag,
  input  xor_flag,
  input  div_flag,
  input  divu_flag,
  input  srl_flag,
  input  or_flag,
  input  remu_flag,
  input  and_flag,
  input  lb_flag,
  input  lh_flag,
  input  lw_flag,
  input  lbu_flag,
  input  lhu_flag,
  input  addi_flag,
  input  slli_flag,
  input  slti_flag,
  input  xori_flag,
  input  srli_flag,
  input  ori_flag,
  input  andi_flag,
  input  sw_flag,
  input  beq_flag,
  input  blt_flag,
  input  bltu_flag,
  input  bne_flag,
  input  bgeu_flag,
  input  auipc_flag,
  input  lui_flag,
  input  jal_flag,
  input  jalr_flag,
  output out_36
);

  wire and_1_out, and_2_out, and_3_out, and_4_out, and_5_out, and_6_out, and_7_out, and_8_out, and_9_out,
       and_10_out, and_11_out, and_12_out, and_13_out, and_14_out, and_15_out, and_16_out, and_17_out,
       and_18_out, and_19_out, and_20_out, and_21_out, and_22_out, and_23_out, and_24_out, and_25_out,
       and_26_out, and_27_out, and_28_out, and_29_out, and_30_out, and_31_out, and_32_out, and_33_out,
       and_34_out, and_35_out, expand_1_1_out_2, expand_1_2_out_2, expand_1_3_out_2, expand_1_4_out_2,
       expand_1_5_out_2, expand_1_6_out_2, expand_1_7_out_2, expand_1_8_out_2, expand_1_9_out_2,
       expand_1_10_out_2, expand_1_11_out_2, expand_1_12_out_2, expand_1_13_out_2, expand_1_14_out_2,
       expand_1_15_out_2, expand_1_16_out_2, expand_1_17_out_2, expand_1_18_out_2, expand_1_19_out_2,
       expand_1_20_out_2, expand_1_21_out_2, expand_1_22_out_2, expand_1_23_out_2, expand_1_24_out_2,
       expand_1_25_out_2, expand_1_26_out_2, expand_1_27_out_2, expand_1_28_out_2, expand_1_29_out_2,
       expand_1_30_out_2, expand_1_31_out_2, expand_1_32_out_2, expand_1_33_out_2, expand_1_34_out_2,
       expand_1_35_out_2, or_1_out;

  expand_1 expand_1_1 (.in_1(add_flag), .out_2(expand_1_1_out_2));
  expand_1 expand_1_2 (.in_1(mul_flag), .out_2(expand_1_2_out_2));
  expand_1 expand_1_3 (.in_1(sub_flag), .out_2(expand_1_3_out_2));
  expand_1 expand_1_4 (.in_1(sll_flag), .out_2(expand_1_4_out_2));
  expand_1 expand_1_5 (.in_1(mulh_flag), .out_2(expand_1_5_out_2));
  expand_1 expand_1_6 (.in_1(mulhu_flag), .out_2(expand_1_6_out_2));
  expand_1 expand_1_7 (.in_1(xor_flag), .out_2(expand_1_7_out_2));
  expand_1 expand_1_8 (.in_1(div_flag), .out_2(expand_1_8_out_2));
  expand_1 expand_1_9 (.in_1(divu_flag), .out_2(expand_1_9_out_2));
  expand_1 expand_1_10 (.in_1(srl_flag), .out_2(expand_1_10_out_2));
  expand_1 expand_1_11 (.in_1(or_flag), .out_2(expand_1_11_out_2));
  expand_1 expand_1_12 (.in_1(remu_flag), .out_2(expand_1_12_out_2));
  expand_1 expand_1_13 (.in_1(and_flag), .out_2(expand_1_13_out_2));
  expand_1 expand_1_14 (.in_1(lb_flag), .out_2(expand_1_14_out_2));
  expand_1 expand_1_15 (.in_1(lh_flag), .out_2(expand_1_15_out_2));
  expand_1 expand_1_16 (.in_1(lw_flag), .out_2(expand_1_16_out_2));
  expand_1 expand_1_17 (.in_1(lbu_flag), .out_2(expand_1_17_out_2));
  expand_1 expand_1_18 (.in_1(lhu_flag), .out_2(expand_1_18_out_2));
  expand_1 expand_1_19 (.in_1(addi_flag), .out_2(expand_1_19_out_2));
  expand_1 expand_1_20 (.in_1(slli_flag), .out_2(expand_1_20_out_2));
  expand_1 expand_1_21 (.in_1(slti_flag), .out_2(expand_1_21_out_2));
  expand_1 expand_1_22 (.in_1(xori_flag), .out_2(expand_1_22_out_2));
  expand_1 expand_1_23 (.in_1(srli_flag), .out_2(expand_1_23_out_2));
  expand_1 expand_1_24 (.in_1(ori_flag), .out_2(expand_1_24_out_2));
  expand_1 expand_1_25 (.in_1(andi_flag), .out_2(expand_1_25_out_2));
  expand_1 expand_1_26 (.in_1(sw_flag), .out_2(expand_1_26_out_2));
  expand_1 expand_1_27 (.in_1(beq_flag), .out_2(expand_1_27_out_2));
  expand_1 expand_1_28 (.in_1(blt_flag), .out_2(expand_1_28_out_2));
  expand_1 expand_1_29 (.in_1(bltu_flag), .out_2(expand_1_29_out_2));
  expand_1 expand_1_30 (.in_1(bne_flag), .out_2(expand_1_30_out_2));
  expand_1 expand_1_31 (.in_1(bgeu_flag), .out_2(expand_1_31_out_2));
  expand_1 expand_1_32 (.in_1(auipc_flag), .out_2(expand_1_32_out_2));
  expand_1 expand_1_33 (.in_1(lui_flag), .out_2(expand_1_33_out_2));
  expand_1 expand_1_34 (.in_1(jal_flag), .out_2(expand_1_34_out_2));
  expand_1 expand_1_35 (.in_1(jalr_flag), .out_2(expand_1_35_out_2));
  and and_1 (and_1_out, expand_1_1_out_2, 1'b0);
  and and_2 (and_2_out, expand_1_2_out_2, 1'b0);
  and and_3 (and_3_out, expand_1_3_out_2, 1'b0);
  and and_4 (and_4_out, expand_1_4_out_2, 1'b0);
  and and_5 (and_5_out, expand_1_5_out_2, 1'b0);
  and and_6 (and_6_out, expand_1_6_out_2, 1'b0);
  and and_7 (and_7_out, expand_1_7_out_2, 1'b0);
  and and_8 (and_8_out, expand_1_8_out_2, 1'b0);
  and and_9 (and_9_out, expand_1_9_out_2, 1'b0);
  and and_10 (and_10_out, expand_1_10_out_2, 1'b0);
  and and_11 (and_11_out, expand_1_11_out_2, 1'b0);
  and and_12 (and_12_out, expand_1_12_out_2, 1'b0);
  and and_13 (and_13_out, expand_1_13_out_2, 1'b0);
  and and_14 (and_14_out, expand_1_14_out_2, 1'b0);
  and and_15 (and_15_out, expand_1_15_out_2, 1'b0);
  and and_16 (and_16_out, expand_1_16_out_2, 1'b0);
  and and_17 (and_17_out, expand_1_17_out_2, 1'b0);
  and and_18 (and_18_out, expand_1_18_out_2, 1'b0);
  and and_19 (and_19_out, expand_1_19_out_2, 1'b0);
  and and_20 (and_20_out, expand_1_20_out_2, 1'b0);
  and and_21 (and_21_out, expand_1_21_out_2, 1'b0);
  and and_22 (and_22_out, expand_1_22_out_2, 1'b0);
  and and_23 (and_23_out, expand_1_23_out_2, 1'b0);
  and and_24 (and_24_out, expand_1_24_out_2, 1'b0);
  and and_25 (and_25_out, expand_1_25_out_2, 1'b0);
  and and_26 (and_26_out, expand_1_26_out_2, 1'b0);
  and and_27 (and_27_out, expand_1_27_out_2, 1'b1);
  and and_28 (and_28_out, expand_1_28_out_2, 1'b1);
  and and_29 (and_29_out, expand_1_29_out_2, 1'b1);
  and and_30 (and_30_out, expand_1_30_out_2, 1'b1);
  and and_31 (and_31_out, expand_1_31_out_2, 1'b1);
  and and_32 (and_32_out, expand_1_32_out_2, 1'b1);
  and and_33 (and_33_out, expand_1_33_out_2, 1'b0);
  and and_34 (and_34_out, expand_1_34_out_2, 1'b1);
  and and_35 (and_35_out, expand_1_35_out_2, 1'b0);
  or or_1 (or_1_out, and_32_out, and_33_out, and_34_out, and_35_out);
  or or_2 (out_36, and_1_out, and_2_out, and_3_out, and_4_out, and_5_out, and_6_out, and_7_out, and_8_out, and_9_out, and_10_out, and_11_out, and_12_out, and_13_out, and_14_out, and_15_out, and_16_out, and_17_out, and_18_out, and_19_out, and_20_out, and_21_out, and_22_out, and_23_out, and_24_out, and_25_out, and_26_out, and_27_out, and_28_out, and_29_out, and_30_out, and_31_out, or_1_out);

  // Notes on the sheet:
  //   Zero presents Reg, One presents PC.
endmodule
module BSel (
  input  add_flag,
  input  mul_flag,
  input  sub_flag,
  input  sll_flag,
  input  mulh_flag,
  input  mulhu_flag,
  input  xor_flag,
  input  div_flag,
  input  divu_flag,
  input  srl_flag,
  input  or_flag,
  input  remu_flag,
  input  and_flag,
  input  lb_flag,
  input  lh_flag,
  input  lw_flag,
  input  lbu_flag,
  input  lhu_flag,
  input  addi_flag,
  input  slli_flag,
  input  slti_flag,
  input  xori_flag,
  input  srli_flag,
  input  ori_flag,
  input  andi_flag,
  input  sw_flag,
  input  beq_flag,
  input  blt_flag,
  input  bltu_flag,
  input  bne_flag,
  input  bgeu_flag,
  input  auipc_flag,
  input  lui_flag,
  input  jal_flag,
  input  jalr_flag,
  output out_36
);

  wire and_1_out, and_2_out, and_3_out, and_4_out, and_5_out, and_6_out, and_7_out, and_8_out, and_9_out,
       and_10_out, and_11_out, and_12_out, and_13_out, and_14_out, and_15_out, and_16_out, and_17_out,
       and_18_out, and_19_out, and_20_out, and_21_out, and_22_out, and_23_out, and_24_out, and_25_out,
       and_26_out, and_27_out, and_28_out, and_29_out, and_30_out, and_31_out, and_32_out, and_33_out,
       and_34_out, and_35_out, expand_1_1_out_2, expand_1_2_out_2, expand_1_3_out_2, expand_1_4_out_2,
       expand_1_5_out_2, expand_1_6_out_2, expand_1_7_out_2, expand_1_8_out_2, expand_1_9_out_2,
       expand_1_10_out_2, expand_1_11_out_2, expand_1_12_out_2, expand_1_13_out_2, expand_1_14_out_2,
       expand_1_15_out_2, expand_1_16_out_2, expand_1_17_out_2, expand_1_18_out_2, expand_1_19_out_2,
       expand_1_20_out_2, expand_1_21_out_2, expand_1_22_out_2, expand_1_23_out_2, expand_1_24_out_2,
       expand_1_25_out_2, expand_1_26_out_2, expand_1_27_out_2, expand_1_28_out_2, expand_1_29_out_2,
       expand_1_30_out_2, expand_1_31_out_2, expand_1_32_out_2, expand_1_33_out_2, expand_1_34_out_2,
       expand_1_35_out_2, or_1_out;

  expand_1 expand_1_1 (.in_1(add_flag), .out_2(expand_1_1_out_2));
  expand_1 expand_1_2 (.in_1(mul_flag), .out_2(expand_1_2_out_2));
  expand_1 expand_1_3 (.in_1(sub_flag), .out_2(expand_1_3_out_2));
  expand_1 expand_1_4 (.in_1(sll_flag), .out_2(expand_1_4_out_2));
  expand_1 expand_1_5 (.in_1(mulh_flag), .out_2(expand_1_5_out_2));
  expand_1 expand_1_6 (.in_1(mulhu_flag), .out_2(expand_1_6_out_2));
  expand_1 expand_1_7 (.in_1(xor_flag), .out_2(expand_1_7_out_2));
  expand_1 expand_1_8 (.in_1(div_flag), .out_2(expand_1_8_out_2));
  expand_1 expand_1_9 (.in_1(divu_flag), .out_2(expand_1_9_out_2));
  expand_1 expand_1_10 (.in_1(srl_flag), .out_2(expand_1_10_out_2));
  expand_1 expand_1_11 (.in_1(or_flag), .out_2(expand_1_11_out_2));
  expand_1 expand_1_12 (.in_1(remu_flag), .out_2(expand_1_12_out_2));
  expand_1 expand_1_13 (.in_1(and_flag), .out_2(expand_1_13_out_2));
  expand_1 expand_1_14 (.in_1(lb_flag), .out_2(expand_1_14_out_2));
  expand_1 expand_1_15 (.in_1(lh_flag), .out_2(expand_1_15_out_2));
  expand_1 expand_1_16 (.in_1(lw_flag), .out_2(expand_1_16_out_2));
  expand_1 expand_1_17 (.in_1(lbu_flag), .out_2(expand_1_17_out_2));
  expand_1 expand_1_18 (.in_1(lhu_flag), .out_2(expand_1_18_out_2));
  expand_1 expand_1_19 (.in_1(addi_flag), .out_2(expand_1_19_out_2));
  expand_1 expand_1_20 (.in_1(slli_flag), .out_2(expand_1_20_out_2));
  expand_1 expand_1_21 (.in_1(slti_flag), .out_2(expand_1_21_out_2));
  expand_1 expand_1_22 (.in_1(xori_flag), .out_2(expand_1_22_out_2));
  expand_1 expand_1_23 (.in_1(srli_flag), .out_2(expand_1_23_out_2));
  expand_1 expand_1_24 (.in_1(ori_flag), .out_2(expand_1_24_out_2));
  expand_1 expand_1_25 (.in_1(andi_flag), .out_2(expand_1_25_out_2));
  expand_1 expand_1_26 (.in_1(sw_flag), .out_2(expand_1_26_out_2));
  expand_1 expand_1_27 (.in_1(beq_flag), .out_2(expand_1_27_out_2));
  expand_1 expand_1_28 (.in_1(blt_flag), .out_2(expand_1_28_out_2));
  expand_1 expand_1_29 (.in_1(bltu_flag), .out_2(expand_1_29_out_2));
  expand_1 expand_1_30 (.in_1(bne_flag), .out_2(expand_1_30_out_2));
  expand_1 expand_1_31 (.in_1(bgeu_flag), .out_2(expand_1_31_out_2));
  expand_1 expand_1_32 (.in_1(auipc_flag), .out_2(expand_1_32_out_2));
  expand_1 expand_1_33 (.in_1(lui_flag), .out_2(expand_1_33_out_2));
  expand_1 expand_1_34 (.in_1(jal_flag), .out_2(expand_1_34_out_2));
  expand_1 expand_1_35 (.in_1(jalr_flag), .out_2(expand_1_35_out_2));
  and and_1 (and_1_out, expand_1_1_out_2, 1'b0);
  and and_2 (and_2_out, expand_1_2_out_2, 1'b0);
  and and_3 (and_3_out, expand_1_3_out_2, 1'b0);
  and and_4 (and_4_out, expand_1_4_out_2, 1'b0);
  and and_5 (and_5_out, expand_1_5_out_2, 1'b0);
  and and_6 (and_6_out, expand_1_6_out_2, 1'b0);
  and and_7 (and_7_out, expand_1_7_out_2, 1'b0);
  and and_8 (and_8_out, expand_1_8_out_2, 1'b0);
  and and_9 (and_9_out, expand_1_9_out_2, 1'b0);
  and and_10 (and_10_out, expand_1_10_out_2, 1'b0);
  and and_11 (and_11_out, expand_1_11_out_2, 1'b0);
  and and_12 (and_12_out, expand_1_12_out_2, 1'b0);
  and and_13 (and_13_out, expand_1_13_out_2, 1'b0);
  and and_14 (and_14_out, expand_1_14_out_2, 1'b1);
  and and_15 (and_15_out, expand_1_15_out_2, 1'b1);
  and and_16 (and_16_out, expand_1_16_out_2, 1'b1);
  and and_17 (and_17_out, expand_1_17_out_2, 1'b1);
  and and_18 (and_18_out, expand_1_18_out_2, 1'b1);
  and and_19 (and_19_out, expand_1_19_out_2, 1'b1);
  and and_20 (and_20_out, expand_1_20_out_2, 1'b1);
  and and_21 (and_21_out, expand_1_21_out_2, 1'b1);
  and and_22 (and_22_out, expand_1_22_out_2, 1'b1);
  and and_23 (and_23_out, expand_1_23_out_2, 1'b1);
  and and_24 (and_24_out, expand_1_24_out_2, 1'b1);
  and and_25 (and_25_out, expand_1_25_out_2, 1'b1);
  and and_26 (and_26_out, expand_1_26_out_2, 1'b1);
  and and_27 (and_27_out, expand_1_27_out_2, 1'b1);
  and and_28 (and_28_out, expand_1_28_out_2, 1'b1);
  and and_29 (and_29_out, expand_1_29_out_2, 1'b1);
  and and_30 (and_30_out, expand_1_30_out_2, 1'b1);
  and and_31 (and_31_out, expand_1_31_out_2, 1'b1);
  and and_32 (and_32_out, expand_1_32_out_2, 1'b1);
  and and_33 (and_33_out, expand_1_33_out_2, 1'b1);
  and and_34 (and_34_out, expand_1_34_out_2, 1'b1);
  and and_35 (and_35_out, expand_1_35_out_2, 1'b1);
  or or_1 (or_1_out, and_32_out, and_33_out, and_34_out, and_35_out);
  or or_2 (out_36, and_1_out, and_2_out, and_3_out, and_4_out, and_5_out, and_6_out, and_7_out, and_8_out, and_9_out, and_10_out, and_11_out, and_12_out, and_13_out, and_14_out, and_15_out, and_16_out, and_17_out, and_18_out, and_19_out, and_20_out, and_21_out, and_22_out, and_23_out, and_24_out, and_25_out, and_26_out, and_27_out, and_28_out, and_29_out, and_30_out, and_31_out, or_1_out);

  // Notes on the sheet:
  //   Zero presents Reg, One presents Imm.
endmodule

module ALUSel (
  input  add_flag,
  input  mul_flag,
  input  sub_flag,
  input  sll_flag,
  input  mulh_flag,
  input  mulhu_flag,
  input  xor_flag,
  input  div_flag,
  input  divu_flag,
  input  srl_flag,
  input  or_flag,
  input  remu_flag,
  input  and_flag,
  input  lb_flag,
  input  lh_flag,
  input  lw_flag,
  input  lbu_flag,
  input  lhu_flag,
  input  addi_flag,
  input  slli_flag,
  input  slti_flag,
  input  xori_flag,
  input  srli_flag,
  input  ori_flag,
  input  andi_flag,
  input  sw_flag,
  input  beq_flag,
  input  blt_flag,
  input  bltu_flag,
  input  bne_flag,
  input  bgeu_flag,
  input  auipc_flag,
  input  lui_flag,
  input  jal_flag,
  input  jalr_flag,
  output [3:0] out_36
);

  wire [3:0] and_1_out, and_2_out, and_3_out, and_4_out, and_5_out, and_6_out, and_7_out, and_8_out,
       and_9_out, and_10_out, and_11_out, and_12_out, and_13_out, and_14_out, and_15_out, and_16_out,
       and_17_out, and_18_out, and_19_out, and_20_out, and_21_out, and_22_out, and_23_out, and_24_out,
       and_25_out, and_26_out, and_27_out, and_28_out, and_29_out, and_30_out, and_31_out, and_32_out,
       and_33_out, and_34_out, and_35_out, expand_4_1_out_2, expand_4_2_out_2, expand_4_3_out_2,
       expand_4_4_out_2, expand_4_5_out_2, expand_4_6_out_2, expand_4_7_out_2, expand_4_8_out_2,
       expand_4_9_out_2, expand_4_10_out_2, expand_4_11_out_2, expand_4_12_out_2, expand_4_13_out_2,
       expand_4_14_out_2, expand_4_15_out_2, expand_4_16_out_2, expand_4_17_out_2, expand_4_18_out_2,
       expand_4_19_out_2, expand_4_20_out_2, expand_4_21_out_2, expand_4_22_out_2, expand_4_23_out_2,
       expand_4_24_out_2, expand_4_25_out_2, expand_4_26_out_2, expand_4_27_out_2, expand_4_28_out_2,
       expand_4_29_out_2, expand_4_30_out_2, expand_4_31_out_2, expand_4_32_out_2, expand_4_33_out_2,
       expand_4_34_out_2, expand_4_35_out_2, or_1_out;

  expand_4 expand_4_1 (.in_1(add_flag), .out_2(expand_4_1_out_2));
  expand_4 expand_4_2 (.in_1(mul_flag), .out_2(expand_4_2_out_2));
  expand_4 expand_4_3 (.in_1(sub_flag), .out_2(expand_4_3_out_2));
  expand_4 expand_4_4 (.in_1(sll_flag), .out_2(expand_4_4_out_2));
  expand_4 expand_4_5 (.in_1(mulh_flag), .out_2(expand_4_5_out_2));
  expand_4 expand_4_6 (.in_1(mulhu_flag), .out_2(expand_4_6_out_2));
  expand_4 expand_4_7 (.in_1(xor_flag), .out_2(expand_4_7_out_2));
  expand_4 expand_4_8 (.in_1(div_flag), .out_2(expand_4_8_out_2));
  expand_4 expand_4_9 (.in_1(divu_flag), .out_2(expand_4_9_out_2));
  expand_4 expand_4_10 (.in_1(srl_flag), .out_2(expand_4_10_out_2));
  expand_4 expand_4_11 (.in_1(or_flag), .out_2(expand_4_11_out_2));
  expand_4 expand_4_12 (.in_1(remu_flag), .out_2(expand_4_12_out_2));
  expand_4 expand_4_13 (.in_1(and_flag), .out_2(expand_4_13_out_2));
  expand_4 expand_4_14 (.in_1(lb_flag), .out_2(expand_4_14_out_2));
  expand_4 expand_4_15 (.in_1(lh_flag), .out_2(expand_4_15_out_2));
  expand_4 expand_4_16 (.in_1(lw_flag), .out_2(expand_4_16_out_2));
  expand_4 expand_4_17 (.in_1(lbu_flag), .out_2(expand_4_17_out_2));
  expand_4 expand_4_18 (.in_1(lhu_flag), .out_2(expand_4_18_out_2));
  expand_4 expand_4_19 (.in_1(addi_flag), .out_2(expand_4_19_out_2));
  expand_4 expand_4_20 (.in_1(slli_flag), .out_2(expand_4_20_out_2));
  expand_4 expand_4_21 (.in_1(slti_flag), .out_2(expand_4_21_out_2));
  expand_4 expand_4_22 (.in_1(xori_flag), .out_2(expand_4_22_out_2));
  expand_4 expand_4_23 (.in_1(srli_flag), .out_2(expand_4_23_out_2));
  expand_4 expand_4_24 (.in_1(ori_flag), .out_2(expand_4_24_out_2));
  expand_4 expand_4_25 (.in_1(andi_flag), .out_2(expand_4_25_out_2));
  expand_4 expand_4_26 (.in_1(sw_flag), .out_2(expand_4_26_out_2));
  expand_4 expand_4_27 (.in_1(beq_flag), .out_2(expand_4_27_out_2));
  expand_4 expand_4_28 (.in_1(blt_flag), .out_2(expand_4_28_out_2));
  expand_4 expand_4_29 (.in_1(bltu_flag), .out_2(expand_4_29_out_2));
  expand_4 expand_4_30 (.in_1(bne_flag), .out_2(expand_4_30_out_2));
  expand_4 expand_4_31 (.in_1(bgeu_flag), .out_2(expand_4_31_out_2));
  expand_4 expand_4_32 (.in_1(auipc_flag), .out_2(expand_4_32_out_2));
  expand_4 expand_4_33 (.in_1(lui_flag), .out_2(expand_4_33_out_2));
  expand_4 expand_4_34 (.in_1(jal_flag), .out_2(expand_4_34_out_2));
  expand_4 expand_4_35 (.in_1(jalr_flag), .out_2(expand_4_35_out_2));
  assign and_1_out = expand_4_1_out_2 & 4'b0011;  // AND_Gate and_1, 4 bits wide
  assign and_2_out = expand_4_2_out_2 & 4'b0101;  // AND_Gate and_2, 4 bits wide
  assign and_3_out = expand_4_3_out_2 & 4'b0100;  // AND_Gate and_3, 4 bits wide
  assign and_4_out = expand_4_4_out_2 & 4'b1110;  // AND_Gate and_4, 4 bits wide
  assign and_5_out = expand_4_5_out_2 & 4'b0111;  // AND_Gate and_5, 4 bits wide
  assign and_6_out = expand_4_6_out_2 & 4'b0110;  // AND_Gate and_6, 4 bits wide
  assign and_7_out = expand_4_7_out_2 & 4'b0010;  // AND_Gate and_7, 4 bits wide
  assign and_8_out = expand_4_8_out_2 & 4'b1001;  // AND_Gate and_8, 4 bits wide
  assign and_9_out = expand_4_9_out_2 & 4'b1000;  // AND_Gate and_9, 4 bits wide
  assign and_10_out = expand_4_10_out_2 & 4'b1011;  // AND_Gate and_10, 4 bits wide
  assign and_11_out = expand_4_11_out_2 & 4'b0001;  // AND_Gate and_11, 4 bits wide
  assign and_12_out = expand_4_12_out_2 & 4'b1010;  // AND_Gate and_12, 4 bits wide
  assign and_13_out = expand_4_13_out_2 & 4'b0000;  // AND_Gate and_13, 4 bits wide
  assign and_14_out = expand_4_14_out_2 & 4'b0011;  // AND_Gate and_14, 4 bits wide
  assign and_15_out = expand_4_15_out_2 & 4'b0011;  // AND_Gate and_15, 4 bits wide
  assign and_16_out = expand_4_16_out_2 & 4'b0011;  // AND_Gate and_16, 4 bits wide
  assign and_17_out = expand_4_17_out_2 & 4'b0011;  // AND_Gate and_17, 4 bits wide
  assign and_18_out = expand_4_18_out_2 & 4'b0011;  // AND_Gate and_18, 4 bits wide
  assign and_19_out = expand_4_19_out_2 & 4'b0011;  // AND_Gate and_19, 4 bits wide
  assign and_20_out = expand_4_20_out_2 & 4'b1110;  // AND_Gate and_20, 4 bits wide
  assign and_21_out = expand_4_21_out_2 & 4'b1101;  // AND_Gate and_21, 4 bits wide
  assign and_22_out = expand_4_22_out_2 & 4'b0010;  // AND_Gate and_22, 4 bits wide
  assign and_23_out = expand_4_23_out_2 & 4'b1011;  // AND_Gate and_23, 4 bits wide
  assign and_24_out = expand_4_24_out_2 & 4'b0001;  // AND_Gate and_24, 4 bits wide
  assign and_25_out = expand_4_25_out_2 & 4'b0000;  // AND_Gate and_25, 4 bits wide
  assign and_26_out = expand_4_26_out_2 & 4'b0011;  // AND_Gate and_26, 4 bits wide
  assign and_27_out = expand_4_27_out_2 & 4'b0011;  // AND_Gate and_27, 4 bits wide
  assign and_28_out = expand_4_28_out_2 & 4'b0011;  // AND_Gate and_28, 4 bits wide
  assign and_29_out = expand_4_29_out_2 & 4'b0011;  // AND_Gate and_29, 4 bits wide
  assign and_30_out = expand_4_30_out_2 & 4'b0011;  // AND_Gate and_30, 4 bits wide
  assign and_31_out = expand_4_31_out_2 & 4'b0011;  // AND_Gate and_31, 4 bits wide
  assign and_32_out = expand_4_32_out_2 & 4'b0011;  // AND_Gate and_32, 4 bits wide
  assign and_33_out = expand_4_33_out_2 & 4'b1111;  // AND_Gate and_33, 4 bits wide
  assign and_34_out = expand_4_34_out_2 & 4'b0011;  // AND_Gate and_34, 4 bits wide
  assign and_35_out = expand_4_35_out_2 & 4'b0011;  // AND_Gate and_35, 4 bits wide
  assign or_1_out = and_32_out | and_33_out | and_34_out | and_35_out;  // OR_Gate or_1, 4 bits wide
  assign out_36 = and_1_out | and_2_out | and_3_out | and_4_out | and_5_out | and_6_out | and_7_out | and_8_out | and_9_out | and_10_out | and_11_out | and_12_out | and_13_out | and_14_out | and_15_out | and_16_out | and_17_out | and_18_out | and_19_out | and_20_out | and_21_out | and_22_out | and_23_out | and_24_out | and_25_out | and_26_out | and_27_out | and_28_out | and_29_out | and_30_out | and_31_out | or_1_out;  // OR_Gate or_2, 4 bits wide
endmodule

module MemRW (
  input  add_flag,
  input  mul_flag,
  input  sub_flag,
  input  sll_flag,
  input  mulh_flag,
  input  mulhu_flag,
  input  xor_flag,
  input  div_flag,
  input  divu_flag,
  input  srl_flag,
  input  or_flag,
  input  remu_flag,
  input  and_flag,
  input  lb_flag,
  input  lh_flag,
  input  lw_flag,
  input  lbu_flag,
  input  lhu_flag,
  input  addi_flag,
  input  slli_flag,
  input  slti_flag,
  input  xori_flag,
  input  srli_flag,
  input  ori_flag,
  input  andi_flag,
  input  sw_flag,
  input  beq_flag,
  input  blt_flag,
  input  bltu_flag,
  input  bne_flag,
  input  bgeu_flag,
  input  auipc_flag,
  input  lui_flag,
  input  jal_flag,
  input  jalr_flag,
  output out_36
);

  wire and_1_out, and_2_out, and_3_out, and_4_out, and_5_out, and_6_out, and_7_out, and_8_out, and_9_out,
       and_10_out, and_11_out, and_12_out, and_13_out, and_14_out, and_15_out, and_16_out, and_17_out,
       and_18_out, and_19_out, and_20_out, and_21_out, and_22_out, and_23_out, and_24_out, and_25_out,
       and_26_out, and_27_out, and_28_out, and_29_out, and_30_out, and_31_out, and_32_out, and_33_out,
       and_34_out, and_35_out, expand_1_1_out_2, expand_1_2_out_2, expand_1_3_out_2, expand_1_4_out_2,
       expand_1_5_out_2, expand_1_6_out_2, expand_1_7_out_2, expand_1_8_out_2, expand_1_9_out_2,
       expand_1_10_out_2, expand_1_11_out_2, expand_1_12_out_2, expand_1_13_out_2, expand_1_14_out_2,
       expand_1_15_out_2, expand_1_16_out_2, expand_1_17_out_2, expand_1_18_out_2, expand_1_19_out_2,
       expand_1_20_out_2, expand_1_21_out_2, expand_1_22_out_2, expand_1_23_out_2, expand_1_24_out_2,
       expand_1_25_out_2, expand_1_26_out_2, expand_1_27_out_2, expand_1_28_out_2, expand_1_29_out_2,
       expand_1_30_out_2, expand_1_31_out_2, expand_1_32_out_2, expand_1_33_out_2, expand_1_34_out_2,
       expand_1_35_out_2, or_1_out;

  expand_1 expand_1_1 (.in_1(add_flag), .out_2(expand_1_1_out_2));
  expand_1 expand_1_2 (.in_1(mul_flag), .out_2(expand_1_2_out_2));
  expand_1 expand_1_3 (.in_1(sub_flag), .out_2(expand_1_3_out_2));
  expand_1 expand_1_4 (.in_1(sll_flag), .out_2(expand_1_4_out_2));
  expand_1 expand_1_5 (.in_1(mulh_flag), .out_2(expand_1_5_out_2));
  expand_1 expand_1_6 (.in_1(mulhu_flag), .out_2(expand_1_6_out_2));
  expand_1 expand_1_7 (.in_1(xor_flag), .out_2(expand_1_7_out_2));
  expand_1 expand_1_8 (.in_1(div_flag), .out_2(expand_1_8_out_2));
  expand_1 expand_1_9 (.in_1(divu_flag), .out_2(expand_1_9_out_2));
  expand_1 expand_1_10 (.in_1(srl_flag), .out_2(expand_1_10_out_2));
  expand_1 expand_1_11 (.in_1(or_flag), .out_2(expand_1_11_out_2));
  expand_1 expand_1_12 (.in_1(remu_flag), .out_2(expand_1_12_out_2));
  expand_1 expand_1_13 (.in_1(and_flag), .out_2(expand_1_13_out_2));
  expand_1 expand_1_14 (.in_1(lb_flag), .out_2(expand_1_14_out_2));
  expand_1 expand_1_15 (.in_1(lh_flag), .out_2(expand_1_15_out_2));
  expand_1 expand_1_16 (.in_1(lw_flag), .out_2(expand_1_16_out_2));
  expand_1 expand_1_17 (.in_1(lbu_flag), .out_2(expand_1_17_out_2));
  expand_1 expand_1_18 (.in_1(lhu_flag), .out_2(expand_1_18_out_2));
  expand_1 expand_1_19 (.in_1(addi_flag), .out_2(expand_1_19_out_2));
  expand_1 expand_1_20 (.in_1(slli_flag), .out_2(expand_1_20_out_2));
  expand_1 expand_1_21 (.in_1(slti_flag), .out_2(expand_1_21_out_2));
  expand_1 expand_1_22 (.in_1(xori_flag), .out_2(expand_1_22_out_2));
  expand_1 expand_1_23 (.in_1(srli_flag), .out_2(expand_1_23_out_2));
  expand_1 expand_1_24 (.in_1(ori_flag), .out_2(expand_1_24_out_2));
  expand_1 expand_1_25 (.in_1(andi_flag), .out_2(expand_1_25_out_2));
  expand_1 expand_1_26 (.in_1(sw_flag), .out_2(expand_1_26_out_2));
  expand_1 expand_1_27 (.in_1(beq_flag), .out_2(expand_1_27_out_2));
  expand_1 expand_1_28 (.in_1(blt_flag), .out_2(expand_1_28_out_2));
  expand_1 expand_1_29 (.in_1(bltu_flag), .out_2(expand_1_29_out_2));
  expand_1 expand_1_30 (.in_1(bne_flag), .out_2(expand_1_30_out_2));
  expand_1 expand_1_31 (.in_1(bgeu_flag), .out_2(expand_1_31_out_2));
  expand_1 expand_1_32 (.in_1(auipc_flag), .out_2(expand_1_32_out_2));
  expand_1 expand_1_33 (.in_1(lui_flag), .out_2(expand_1_33_out_2));
  expand_1 expand_1_34 (.in_1(jal_flag), .out_2(expand_1_34_out_2));
  expand_1 expand_1_35 (.in_1(jalr_flag), .out_2(expand_1_35_out_2));
  and and_1 (and_1_out, expand_1_1_out_2, 1'b0);
  and and_2 (and_2_out, expand_1_2_out_2, 1'b0);
  and and_3 (and_3_out, expand_1_3_out_2, 1'b0);
  and and_4 (and_4_out, expand_1_4_out_2, 1'b0);
  and and_5 (and_5_out, expand_1_5_out_2, 1'b0);
  and and_6 (and_6_out, expand_1_6_out_2, 1'b0);
  and and_7 (and_7_out, expand_1_7_out_2, 1'b0);
  and and_8 (and_8_out, expand_1_8_out_2, 1'b0);
  and and_9 (and_9_out, expand_1_9_out_2, 1'b0);
  and and_10 (and_10_out, expand_1_10_out_2, 1'b0);
  and and_11 (and_11_out, expand_1_11_out_2, 1'b0);
  and and_12 (and_12_out, expand_1_12_out_2, 1'b0);
  and and_13 (and_13_out, expand_1_13_out_2, 1'b0);
  and and_14 (and_14_out, expand_1_14_out_2, 1'b0);
  and and_15 (and_15_out, expand_1_15_out_2, 1'b0);
  and and_16 (and_16_out, expand_1_16_out_2, 1'b0);
  and and_17 (and_17_out, expand_1_17_out_2, 1'b0);
  and and_18 (and_18_out, expand_1_18_out_2, 1'b0);
  and and_19 (and_19_out, expand_1_19_out_2, 1'b0);
  and and_20 (and_20_out, expand_1_20_out_2, 1'b0);
  and and_21 (and_21_out, expand_1_21_out_2, 1'b0);
  and and_22 (and_22_out, expand_1_22_out_2, 1'b0);
  and and_23 (and_23_out, expand_1_23_out_2, 1'b0);
  and and_24 (and_24_out, expand_1_24_out_2, 1'b0);
  and and_25 (and_25_out, expand_1_25_out_2, 1'b0);
  and and_26 (and_26_out, expand_1_26_out_2, 1'b1);
  and and_27 (and_27_out, expand_1_27_out_2, 1'b0);
  and and_28 (and_28_out, expand_1_28_out_2, 1'b0);
  and and_29 (and_29_out, expand_1_29_out_2, 1'b0);
  and and_30 (and_30_out, expand_1_30_out_2, 1'b0);
  and and_31 (and_31_out, expand_1_31_out_2, 1'b0);
  and and_32 (and_32_out, expand_1_32_out_2, 1'b0);
  and and_33 (and_33_out, expand_1_33_out_2, 1'b0);
  and and_34 (and_34_out, expand_1_34_out_2, 1'b0);
  and and_35 (and_35_out, expand_1_35_out_2, 1'b0);
  or or_1 (or_1_out, and_32_out, and_33_out, and_34_out, and_35_out);
  or or_2 (out_36, and_1_out, and_2_out, and_3_out, and_4_out, and_5_out, and_6_out, and_7_out, and_8_out, and_9_out, and_10_out, and_11_out, and_12_out, and_13_out, and_14_out, and_15_out, and_16_out, and_17_out, and_18_out, and_19_out, and_20_out, and_21_out, and_22_out, and_23_out, and_24_out, and_25_out, and_26_out, and_27_out, and_28_out, and_29_out, and_30_out, and_31_out, or_1_out);
endmodule

module RegWEn (
  input  add_flag,
  input  mul_flag,
  input  sub_flag,
  input  sll_flag,
  input  mulh_flag,
  input  mulhu_flag,
  input  xor_flag,
  input  div_flag,
  input  divu_flag,
  input  srl_flag,
  input  or_flag,
  input  remu_flag,
  input  and_flag,
  input  lb_flag,
  input  lh_flag,
  input  lw_flag,
  input  lbu_flag,
  input  lhu_flag,
  input  addi_flag,
  input  slli_flag,
  input  slti_flag,
  input  xori_flag,
  input  srli_flag,
  input  ori_flag,
  input  andi_flag,
  input  sw_flag,
  input  beq_flag,
  input  blt_flag,
  input  bltu_flag,
  input  bne_flag,
  input  bgeu_flag,
  input  auipc_flag,
  input  lui_flag,
  input  jal_flag,
  input  jalr_flag,
  output out_36
);

  wire and_1_out, and_2_out, and_3_out, and_4_out, and_5_out, and_6_out, and_7_out, and_8_out, and_9_out,
       and_10_out, and_11_out, and_12_out, and_13_out, and_14_out, and_15_out, and_16_out, and_17_out,
       and_18_out, and_19_out, and_20_out, and_21_out, and_22_out, and_23_out, and_24_out, and_25_out,
       and_26_out, and_27_out, and_28_out, and_29_out, and_30_out, and_31_out, and_32_out, and_33_out,
       and_34_out, and_35_out, expand_1_1_out_2, expand_1_2_out_2, expand_1_3_out_2, expand_1_4_out_2,
       expand_1_5_out_2, expand_1_6_out_2, expand_1_7_out_2, expand_1_8_out_2, expand_1_9_out_2,
       expand_1_10_out_2, expand_1_11_out_2, expand_1_12_out_2, expand_1_13_out_2, expand_1_14_out_2,
       expand_1_15_out_2, expand_1_16_out_2, expand_1_17_out_2, expand_1_18_out_2, expand_1_19_out_2,
       expand_1_20_out_2, expand_1_21_out_2, expand_1_22_out_2, expand_1_23_out_2, expand_1_24_out_2,
       expand_1_25_out_2, expand_1_26_out_2, expand_1_27_out_2, expand_1_28_out_2, expand_1_29_out_2,
       expand_1_30_out_2, expand_1_31_out_2, expand_1_32_out_2, expand_1_33_out_2, expand_1_34_out_2,
       expand_1_35_out_2, or_1_out;

  expand_1 expand_1_1 (.in_1(add_flag), .out_2(expand_1_1_out_2));
  expand_1 expand_1_2 (.in_1(mul_flag), .out_2(expand_1_2_out_2));
  expand_1 expand_1_3 (.in_1(sub_flag), .out_2(expand_1_3_out_2));
  expand_1 expand_1_4 (.in_1(sll_flag), .out_2(expand_1_4_out_2));
  expand_1 expand_1_5 (.in_1(mulh_flag), .out_2(expand_1_5_out_2));
  expand_1 expand_1_6 (.in_1(mulhu_flag), .out_2(expand_1_6_out_2));
  expand_1 expand_1_7 (.in_1(xor_flag), .out_2(expand_1_7_out_2));
  expand_1 expand_1_8 (.in_1(div_flag), .out_2(expand_1_8_out_2));
  expand_1 expand_1_9 (.in_1(divu_flag), .out_2(expand_1_9_out_2));
  expand_1 expand_1_10 (.in_1(srl_flag), .out_2(expand_1_10_out_2));
  expand_1 expand_1_11 (.in_1(or_flag), .out_2(expand_1_11_out_2));
  expand_1 expand_1_12 (.in_1(remu_flag), .out_2(expand_1_12_out_2));
  expand_1 expand_1_13 (.in_1(and_flag), .out_2(expand_1_13_out_2));
  expand_1 expand_1_14 (.in_1(lb_flag), .out_2(expand_1_14_out_2));
  expand_1 expand_1_15 (.in_1(lh_flag), .out_2(expand_1_15_out_2));
  expand_1 expand_1_16 (.in_1(lw_flag), .out_2(expand_1_16_out_2));
  expand_1 expand_1_17 (.in_1(lbu_flag), .out_2(expand_1_17_out_2));
  expand_1 expand_1_18 (.in_1(lhu_flag), .out_2(expand_1_18_out_2));
  expand_1 expand_1_19 (.in_1(addi_flag), .out_2(expand_1_19_out_2));
  expand_1 expand_1_20 (.in_1(slli_flag), .out_2(expand_1_20_out_2));
  expand_1 expand_1_21 (.in_1(slti_flag), .out_2(expand_1_21_out_2));
  expand_1 expand_1_22 (.in_1(xori_flag), .out_2(expand_1_22_out_2));
  expand_1 expand_1_23 (.in_1(srli_flag), .out_2(expand_1_23_out_2));
  expand_1 expand_1_24 (.in_1(ori_flag), .out_2(expand_1_24_out_2));
  expand_1 expand_1_25 (.in_1(andi_flag), .out_2(expand_1_25_out_2));
  expand_1 expand_1_26 (.in_1(sw_flag), .out_2(expand_1_26_out_2));
  expand_1 expand_1_27 (.in_1(beq_flag), .out_2(expand_1_27_out_2));
  expand_1 expand_1_28 (.in_1(blt_flag), .out_2(expand_1_28_out_2));
  expand_1 expand_1_29 (.in_1(bltu_flag), .out_2(expand_1_29_out_2));
  expand_1 expand_1_30 (.in_1(bne_flag), .out_2(expand_1_30_out_2));
  expand_1 expand_1_31 (.in_1(bgeu_flag), .out_2(expand_1_31_out_2));
  expand_1 expand_1_32 (.in_1(auipc_flag), .out_2(expand_1_32_out_2));
  expand_1 expand_1_33 (.in_1(lui_flag), .out_2(expand_1_33_out_2));
  expand_1 expand_1_34 (.in_1(jal_flag), .out_2(expand_1_34_out_2));
  expand_1 expand_1_35 (.in_1(jalr_flag), .out_2(expand_1_35_out_2));
  and and_1 (and_1_out, expand_1_1_out_2, 1'b1);
  and and_2 (and_2_out, expand_1_2_out_2, 1'b1);
  and and_3 (and_3_out, expand_1_3_out_2, 1'b1);
  and and_4 (and_4_out, expand_1_4_out_2, 1'b1);
  and and_5 (and_5_out, expand_1_5_out_2, 1'b1);
  and and_6 (and_6_out, expand_1_6_out_2, 1'b1);
  and and_7 (and_7_out, expand_1_7_out_2, 1'b1);
  and and_8 (and_8_out, expand_1_8_out_2, 1'b1);
  and and_9 (and_9_out, expand_1_9_out_2, 1'b1);
  and and_10 (and_10_out, expand_1_10_out_2, 1'b1);
  and and_11 (and_11_out, expand_1_11_out_2, 1'b1);
  and and_12 (and_12_out, expand_1_12_out_2, 1'b1);
  and and_13 (and_13_out, expand_1_13_out_2, 1'b1);
  and and_14 (and_14_out, expand_1_14_out_2, 1'b1);
  and and_15 (and_15_out, expand_1_15_out_2, 1'b1);
  and and_16 (and_16_out, expand_1_16_out_2, 1'b1);
  and and_17 (and_17_out, expand_1_17_out_2, 1'b1);
  and and_18 (and_18_out, expand_1_18_out_2, 1'b1);
  and and_19 (and_19_out, expand_1_19_out_2, 1'b1);
  and and_20 (and_20_out, expand_1_20_out_2, 1'b1);
  and and_21 (and_21_out, expand_1_21_out_2, 1'b1);
  and and_22 (and_22_out, expand_1_22_out_2, 1'b1);
  and and_23 (and_23_out, expand_1_23_out_2, 1'b1);
  and and_24 (and_24_out, expand_1_24_out_2, 1'b1);
  and and_25 (and_25_out, expand_1_25_out_2, 1'b1);
  and and_26 (and_26_out, expand_1_26_out_2, 1'b0);
  and and_27 (and_27_out, expand_1_27_out_2, 1'b0);
  and and_28 (and_28_out, expand_1_28_out_2, 1'b0);
  and and_29 (and_29_out, expand_1_29_out_2, 1'b0);
  and and_30 (and_30_out, expand_1_30_out_2, 1'b0);
  and and_31 (and_31_out, expand_1_31_out_2, 1'b0);
  and and_32 (and_32_out, expand_1_32_out_2, 1'b1);
  and and_33 (and_33_out, expand_1_33_out_2, 1'b1);
  and and_34 (and_34_out, expand_1_34_out_2, 1'b1);
  and and_35 (and_35_out, expand_1_35_out_2, 1'b1);
  or or_1 (or_1_out, and_32_out, and_33_out, and_34_out, and_35_out);
  or or_2 (out_36, and_1_out, and_2_out, and_3_out, and_4_out, and_5_out, and_6_out, and_7_out, and_8_out, and_9_out, and_10_out, and_11_out, and_12_out, and_13_out, and_14_out, and_15_out, and_16_out, and_17_out, and_18_out, and_19_out, and_20_out, and_21_out, and_22_out, and_23_out, and_24_out, and_25_out, and_26_out, and_27_out, and_28_out, and_29_out, and_30_out, and_31_out, or_1_out);
endmodule

module WBSel (
  input  add_flag,
  input  mul_flag,
  input  sub_flag,
  input  sll_flag,
  input  mulh_flag,
  input  mulhu_flag,
  input  xor_flag,
  input  div_flag,
  input  divu_flag,
  input  srl_flag,
  input  or_flag,
  input  remu_flag,
  input  and_flag,
  input  lb_flag,
  input  lh_flag,
  input  lw_flag,
  input  lbu_flag,
  input  lhu_flag,
  input  addi_flag,
  input  slli_flag,
  input  slti_flag,
  input  xori_flag,
  input  srli_flag,
  input  ori_flag,
  input  andi_flag,
  input  sw_flag,
  input  beq_flag,
  input  blt_flag,
  input  bltu_flag,
  input  bne_flag,
  input  bgeu_flag,
  input  auipc_flag,
  input  lui_flag,
  input  jal_flag,
  input  jalr_flag,
  output [1:0] out_36
);

  wire [1:0] and_1_out, and_2_out, and_3_out, and_4_out, and_5_out, and_6_out, and_7_out, and_8_out,
       and_9_out, and_10_out, and_11_out, and_12_out, and_13_out, and_14_out, and_15_out, and_16_out,
       and_17_out, and_18_out, and_19_out, and_20_out, and_21_out, and_22_out, and_23_out, and_24_out,
       and_25_out, and_26_out, and_27_out, and_28_out, and_29_out, and_30_out, and_31_out, and_32_out,
       and_33_out, and_34_out, and_35_out, expand_2_1_out_2, expand_2_2_out_2, expand_2_3_out_2,
       expand_2_4_out_2, expand_2_5_out_2, expand_2_6_out_2, expand_2_7_out_2, expand_2_8_out_2,
       expand_2_9_out_2, expand_2_10_out_2, expand_2_11_out_2, expand_2_12_out_2, expand_2_13_out_2,
       expand_2_14_out_2, expand_2_15_out_2, expand_2_16_out_2, expand_2_17_out_2, expand_2_18_out_2,
       expand_2_19_out_2, expand_2_20_out_2, expand_2_21_out_2, expand_2_22_out_2, expand_2_23_out_2,
       expand_2_24_out_2, expand_2_25_out_2, expand_2_26_out_2, expand_2_27_out_2, expand_2_28_out_2,
       expand_2_29_out_2, expand_2_30_out_2, expand_2_31_out_2, expand_2_32_out_2, expand_2_33_out_2,
       expand_2_34_out_2, expand_2_35_out_2, or_1_out;

  expand_2 expand_2_1 (.in_1(add_flag), .out_2(expand_2_1_out_2));
  expand_2 expand_2_2 (.in_1(mul_flag), .out_2(expand_2_2_out_2));
  expand_2 expand_2_3 (.in_1(sub_flag), .out_2(expand_2_3_out_2));
  expand_2 expand_2_4 (.in_1(sll_flag), .out_2(expand_2_4_out_2));
  expand_2 expand_2_5 (.in_1(mulh_flag), .out_2(expand_2_5_out_2));
  expand_2 expand_2_6 (.in_1(mulhu_flag), .out_2(expand_2_6_out_2));
  expand_2 expand_2_7 (.in_1(xor_flag), .out_2(expand_2_7_out_2));
  expand_2 expand_2_8 (.in_1(div_flag), .out_2(expand_2_8_out_2));
  expand_2 expand_2_9 (.in_1(divu_flag), .out_2(expand_2_9_out_2));
  expand_2 expand_2_10 (.in_1(srl_flag), .out_2(expand_2_10_out_2));
  expand_2 expand_2_11 (.in_1(or_flag), .out_2(expand_2_11_out_2));
  expand_2 expand_2_12 (.in_1(remu_flag), .out_2(expand_2_12_out_2));
  expand_2 expand_2_13 (.in_1(and_flag), .out_2(expand_2_13_out_2));
  expand_2 expand_2_14 (.in_1(lb_flag), .out_2(expand_2_14_out_2));
  expand_2 expand_2_15 (.in_1(lh_flag), .out_2(expand_2_15_out_2));
  expand_2 expand_2_16 (.in_1(lw_flag), .out_2(expand_2_16_out_2));
  expand_2 expand_2_17 (.in_1(lbu_flag), .out_2(expand_2_17_out_2));
  expand_2 expand_2_18 (.in_1(lhu_flag), .out_2(expand_2_18_out_2));
  expand_2 expand_2_19 (.in_1(addi_flag), .out_2(expand_2_19_out_2));
  expand_2 expand_2_20 (.in_1(slli_flag), .out_2(expand_2_20_out_2));
  expand_2 expand_2_21 (.in_1(slti_flag), .out_2(expand_2_21_out_2));
  expand_2 expand_2_22 (.in_1(xori_flag), .out_2(expand_2_22_out_2));
  expand_2 expand_2_23 (.in_1(srli_flag), .out_2(expand_2_23_out_2));
  expand_2 expand_2_24 (.in_1(ori_flag), .out_2(expand_2_24_out_2));
  expand_2 expand_2_25 (.in_1(andi_flag), .out_2(expand_2_25_out_2));
  expand_2 expand_2_26 (.in_1(sw_flag), .out_2(expand_2_26_out_2));
  expand_2 expand_2_27 (.in_1(beq_flag), .out_2(expand_2_27_out_2));
  expand_2 expand_2_28 (.in_1(blt_flag), .out_2(expand_2_28_out_2));
  expand_2 expand_2_29 (.in_1(bltu_flag), .out_2(expand_2_29_out_2));
  expand_2 expand_2_30 (.in_1(bne_flag), .out_2(expand_2_30_out_2));
  expand_2 expand_2_31 (.in_1(bgeu_flag), .out_2(expand_2_31_out_2));
  expand_2 expand_2_32 (.in_1(auipc_flag), .out_2(expand_2_32_out_2));
  expand_2 expand_2_33 (.in_1(lui_flag), .out_2(expand_2_33_out_2));
  expand_2 expand_2_34 (.in_1(jal_flag), .out_2(expand_2_34_out_2));
  expand_2 expand_2_35 (.in_1(jalr_flag), .out_2(expand_2_35_out_2));
  assign and_1_out = expand_2_1_out_2 & 2'b00;  // AND_Gate and_1, 2 bits wide
  assign and_2_out = expand_2_2_out_2 & 2'b00;  // AND_Gate and_2, 2 bits wide
  assign and_3_out = expand_2_3_out_2 & 2'b00;  // AND_Gate and_3, 2 bits wide
  assign and_4_out = expand_2_4_out_2 & 2'b00;  // AND_Gate and_4, 2 bits wide
  assign and_5_out = expand_2_5_out_2 & 2'b00;  // AND_Gate and_5, 2 bits wide
  assign and_6_out = expand_2_6_out_2 & 2'b00;  // AND_Gate and_6, 2 bits wide
  assign and_7_out = expand_2_7_out_2 & 2'b00;  // AND_Gate and_7, 2 bits wide
  assign and_8_out = expand_2_8_out_2 & 2'b00;  // AND_Gate and_8, 2 bits wide
  assign and_9_out = expand_2_9_out_2 & 2'b00;  // AND_Gate and_9, 2 bits wide
  assign and_10_out = expand_2_10_out_2 & 2'b00;  // AND_Gate and_10, 2 bits wide
  assign and_11_out = expand_2_11_out_2 & 2'b00;  // AND_Gate and_11, 2 bits wide
  assign and_12_out = expand_2_12_out_2 & 2'b00;  // AND_Gate and_12, 2 bits wide
  assign and_13_out = expand_2_13_out_2 & 2'b00;  // AND_Gate and_13, 2 bits wide
  assign and_14_out = expand_2_14_out_2 & 2'b00;  // AND_Gate and_14, 2 bits wide
  assign and_15_out = expand_2_15_out_2 & 2'b00;  // AND_Gate and_15, 2 bits wide
  assign and_16_out = expand_2_16_out_2 & 2'b01;  // AND_Gate and_16, 2 bits wide
  assign and_17_out = expand_2_17_out_2 & 2'b00;  // AND_Gate and_17, 2 bits wide
  assign and_18_out = expand_2_18_out_2 & 2'b00;  // AND_Gate and_18, 2 bits wide
  assign and_19_out = expand_2_19_out_2 & 2'b00;  // AND_Gate and_19, 2 bits wide
  assign and_20_out = expand_2_20_out_2 & 2'b00;  // AND_Gate and_20, 2 bits wide
  assign and_21_out = expand_2_21_out_2 & 2'b00;  // AND_Gate and_21, 2 bits wide
  assign and_22_out = expand_2_22_out_2 & 2'b00;  // AND_Gate and_22, 2 bits wide
  assign and_23_out = expand_2_23_out_2 & 2'b00;  // AND_Gate and_23, 2 bits wide
  assign and_24_out = expand_2_24_out_2 & 2'b00;  // AND_Gate and_24, 2 bits wide
  assign and_25_out = expand_2_25_out_2 & 2'b00;  // AND_Gate and_25, 2 bits wide
  assign and_26_out = expand_2_26_out_2 & 2'b00;  // AND_Gate and_26, 2 bits wide
  assign and_27_out = expand_2_27_out_2 & 2'b00;  // AND_Gate and_27, 2 bits wide
  assign and_28_out = expand_2_28_out_2 & 2'b00;  // AND_Gate and_28, 2 bits wide
  assign and_29_out = expand_2_29_out_2 & 2'b00;  // AND_Gate and_29, 2 bits wide
  assign and_30_out = expand_2_30_out_2 & 2'b00;  // AND_Gate and_30, 2 bits wide
  assign and_31_out = expand_2_31_out_2 & 2'b00;  // AND_Gate and_31, 2 bits wide
  assign and_32_out = expand_2_32_out_2 & 2'b00;  // AND_Gate and_32, 2 bits wide
  assign and_33_out = expand_2_33_out_2 & 2'b00;  // AND_Gate and_33, 2 bits wide
  assign and_34_out = expand_2_34_out_2 & 2'b10;  // AND_Gate and_34, 2 bits wide
  assign and_35_out = expand_2_35_out_2 & 2'b10;  // AND_Gate and_35, 2 bits wide
  assign or_1_out = and_32_out | and_33_out | and_34_out | and_35_out;  // OR_Gate or_1, 2 bits wide
  assign out_36 = and_1_out | and_2_out | and_3_out | and_4_out | and_5_out | and_6_out | and_7_out | and_8_out | and_9_out | and_10_out | and_11_out | and_12_out | and_13_out | and_14_out | and_15_out | and_16_out | and_17_out | and_18_out | and_19_out | and_20_out | and_21_out | and_22_out | and_23_out | and_24_out | and_25_out | and_26_out | and_27_out | and_28_out | and_29_out | and_30_out | and_31_out | or_1_out;  // OR_Gate or_2, 2 bits wide

  // Notes on the sheet:
  //   Zero presents Unsigned and ALU, One presents Mem, Two presents PC + 4.
endmodule

module expand_4 (
  input  in_1,
  output [3:0] out_2
);


  assign out_2 = {4{in_1}};
endmodule

module expand_3 (
  input  in_1,
  output [2:0] out_2
);


  assign out_2 = {3{in_1}};
endmodule

module expand_2 (
  input  in_1,
  output [1:0] out_2
);


  assign out_2 = {2{in_1}};
endmodule

module expand_1 (
  input  in_1,
  output out_2
);


  assign out_2 = in_1;
endmodule

module imm_gen (
  input  [31:0] ins,
  input  [2:0] immSel,
  output [31:0] imm_ans
);

  wire [31:0] b_imm_1_b_imm_ans, i_imm_1_i_imm_ans, j_imm_1_j_imm_ans, s_imm_1_s_imm_ans, u_imm_1_u_imm_ans;

  I_imm i_imm_1 (.ins(ins), .I_imm_ans(i_imm_1_i_imm_ans));
  S_imm s_imm_1 (.ins(ins), .S_imm_ans(s_imm_1_s_imm_ans));
  B_imm b_imm_1 (.ins(ins), .B_imm_ans(b_imm_1_b_imm_ans));
  U_imm u_imm_1 (.ins(ins), .U_imm_ans(u_imm_1_u_imm_ans));
  J_imm j_imm_1 (.ins(ins), .J_imm_ans(j_imm_1_j_imm_ans));
  Multiplexer #(.select(3), .width(32), .enable("false")) multiplexer_1 (
    .in0(i_imm_1_i_imm_ans), .in1(s_imm_1_s_imm_ans), .in2(b_imm_1_b_imm_ans), .in3(j_imm_1_j_imm_ans),
    .in4(u_imm_1_u_imm_ans), .out(imm_ans), .sel(immSel));  // open: in5, in6, in7

  // Other names for the same wires on the sheet: ins_in[31:0] = ins
endmodule

module I_imm (
  input  [31:0] ins,
  output [31:0] I_imm_ans
);


  assign I_imm_ans = {{21{ins[31]}}, ins[30:20]};
endmodule

module S_imm (
  input  [31:0] ins,
  output [31:0] S_imm_ans
);


  assign S_imm_ans = {{21{ins[31]}}, ins[30:25], ins[11:7]};
endmodule

module B_imm (
  input  [31:0] ins,
  output [31:0] B_imm_ans
);


  assign B_imm_ans = {{20{ins[31]}}, ins[7], ins[30:25], ins[11:8], 1'b0};
endmodule

module U_imm (
  input  [31:0] ins,
  output [31:0] U_imm_ans
);


  assign U_imm_ans = {ins[31:12], {12{1'b0}}};
endmodule

module J_imm (
  input  [31:0] ins,
  output [31:0] J_imm_ans
);


  assign J_imm_ans = {{12{ins[31]}}, ins[19:12], ins[20], ins[30:21], 1'b0};
endmodule

module get_opcode_from_ins (
  input  [31:0] ins,
  output [6:0] opcode
);


  assign opcode = ins[6:0];
endmodule

module BranchComp (
  input  [31:0] DataA,
  input  [31:0] DataB,
  input  BrUn,
  output BrEq,
  output BrLT
);

  wire comparator_1_eq, comparator_2_eq, comparator_3_lt, comparator_4_lt;

  Comparator #(.width(32)) comparator_1 (.a(DataA), .b(DataB), .eq(comparator_1_eq));  // open: gt, lt
  Comparator #(.width(32), .mode("unsigned")) comparator_2 (
    .a(DataA), .b(DataB), .eq(comparator_2_eq));  // open: gt, lt
  Comparator #(.width(32)) comparator_3 (.a(DataA), .b(DataB), .lt(comparator_3_lt));  // open: gt, eq
  Comparator #(.width(32), .mode("unsigned")) comparator_4 (
    .a(DataA), .b(DataB), .lt(comparator_4_lt));  // open: gt, eq
  Multiplexer #(.enable("false")) multiplexer_1 (.in0(comparator_1_eq), .in1(comparator_2_eq), .out(BrEq), .sel(BrUn));
  Multiplexer #(.enable("false")) multiplexer_2 (.in0(comparator_3_lt), .in1(comparator_4_lt), .out(BrLT), .sel(BrUn));
endmodule
