// Logisim project gen_imm.circ as structural Verilog: 7 circuits, main circuit imm_gen
module imm_gen (
  input  [31:0] ins,
  output [31:0] imm_ans
);

  wire B_sel, comparator_1_eq, comparator_2_eq, comparator_3_eq, comparator_6_eq, comparator_7_eq, I_sel,
       J_sel, S_sel, U_sel;
  wire [6:0] Opcode;
  wire [31:0] b_imm_1_b_imm_ans, i_imm_1_i_imm_ans, j_imm_1_j_imm_ans, s_imm_1_s_imm_ans, u_imm_1_u_imm_ans;

  Comparator #(.width(7)) comparator_1 (.a(Opcode), .b(7'b0000011), .eq(comparator_1_eq));  // open: gt, lt
  Comparator #(.width(7)) comparator_2 (.a(Opcode), .b(7'b0010011), .eq(comparator_2_eq));  // open: gt, lt
  Comparator #(.width(7)) comparator_3 (.a(Opcode), .b(7'b1100111), .eq(comparator_3_eq));  // open: gt, lt
  Comparator #(.width(7)) comparator_4 (.a(Opcode), .b(7'b0100011), .eq(S_sel));  // open: gt, lt
  Comparator #(.width(7)) comparator_5 (.a(Opcode), .b(7'b1100011), .eq(B_sel));  // open: gt, lt
  Comparator #(.width(7)) comparator_6 (.a(Opcode), .b(7'b0010111), .eq(comparator_6_eq));  // open: gt, lt
  Comparator #(.width(7)) comparator_7 (.a(Opcode), .b(7'b0110111), .eq(comparator_7_eq));  // open: gt, lt
  Comparator #(.width(7)) comparator_8 (.a(Opcode), .b(7'b1101111), .eq(J_sel));  // open: gt, lt
  or or_1 (I_sel, comparator_1_eq, comparator_3_eq, comparator_2_eq);
  or or_2 (U_sel, comparator_6_eq, comparator_7_eq);
  get_opcode_from_ins get_opcode_from_ins_1 (.ins(ins), .opcode(Opcode));
  I_imm i_imm_1 (.ins(ins), .I_imm_ans(i_imm_1_i_imm_ans));
  S_imm s_imm_1 (.ins(ins), .S_imm_ans(s_imm_1_s_imm_ans));
  B_imm b_imm_1 (.ins(ins), .B_imm_ans(b_imm_1_b_imm_ans));
  U_imm u_imm_1 (.ins(ins), .U_imm_ans(u_imm_1_u_imm_ans));
  J_imm j_imm_1 (.ins(ins), .J_imm_ans(j_imm_1_j_imm_ans));
  Multiplexer #(.select(5), .width(32), .enable("false")) multiplexer_1 (
    .in1(i_imm_1_i_imm_ans), .in2(s_imm_1_s_imm_ans), .in4(b_imm_1_b_imm_ans), .in8(u_imm_1_u_imm_ans),
    .in16(j_imm_1_j_imm_ans), .out(imm_ans), .sel({J_sel, U_sel, B_sel, S_sel, I_sel}));  // open: in0, in3, in5, in6, in7, in9, in10, in11, in12, in13, in14, in15, in17, in18, in19, in20, in21, in22, in23, in24, in25, in26, in27, in28, in29, in30, in31

  // Other names for the same wires on the sheet: ins_in[31:0] = ins
endmodule

module I_imm (
  input  [31:0] ins,
  output [31:0] I_imm_ans
);


  assign I_imm_ans = {{21{ins[31]}}, ins[30:20]};
endmodule

module S_imm (
  input  [31:0] ins,
  output [31:0] S_imm_ans
);


  assign S_imm_ans = {{21{ins[31]}}, ins[30:25], ins[11:7]};
endmodule

module B_imm (
  input  [31:0] ins,
  output [31:0] B_imm_ans
);


  assign B_imm_ans = {{20{ins[31]}}, ins[7], ins[30:25], ins[11:8], 1'b0};
endmodule

module U_imm (
  input  [31:0] ins,
  output [31:0] U_imm_ans
);


  assign U_imm_ans = {ins[31:12], {12{1'b0}}};
endmodule

module J_imm (
  input  [31:0] ins,
  output [31:0] J_imm_ans
);


  assign J_imm_ans = {{12{ins[31]}}, ins[19:12], ins[20], ins[30:21], 1'b0};
endmodule

module get_opcode_from_ins (
  input  [31:0] ins,
  output [6:0] opcode
);


  assign opcode = ins[6:0];
endmodule
